// Logisim project processor.circ as structural Verilog: 25 circuits, main circuit main
module main (
  input  reset
);

  wire ALUinB, ALUopAddC, and_1_out, and_4_out, and_10_out, and_11_out, and_15_out, BEXC, BEXC_X, BLT, BLTC,
       BNE, BNEC, comparator_1_eq, comparator_2_eq, comparator_3_eq, comparator_4_gt, comparator_4_lt,
       comparator_5_eq, comparator_6_eq, comparator_7_eq, comparator_8_eq, comparator_9_eq, comparator_10_eq,
       comparator_11_eq, comparator_12_eq, d_ff_1_q, d_ff_2_q, data_resultRDY, div_progress, div_start, DMld,
       DMwe, fall, flush_signal, JalC, m_w_1_swc_mw, MEMwrite, mult_progress, mult_start, multdiv_div_rdy,
       multdiv_mult_rdy, not_3_out, not_5_out, not_6_out, not_7_out, not_stall, not_stall_DX, not_stall_FD,
       or_1_out, or_2_out, or_3_out, or_5_out, or_7_out, ovf, PConeNC, PConeNCR, PCRdC, PCTC, PCTCR, RdC,
       rise, RsC, RstatusC, Rwe, SETXC_D, SETXC_X, stall_DX, stall_FD, stall_lw_bypass, SwC, SwC_MW_Not,
       SwC_XM_Not, x_m_1_swc_xm;
  wire [1:1] and_14_out;
  wire [2:1] and_2_out, and_6_out;
  wire [4:0] ALUop, multiplexer_1_out, multiplexer_2_out, multiplexer_4_out, multiplexer_6_out,
       multiplexer_8_out, multiplexer_9_out, multiplexer_10_out, multiplexer_16_out, Opcode_DX, Opcode_FD,
       Rd, Rd_DX_bypass, Rd_MW, Rd_MW_bypass, Rd_XM_bypass, Rs, Rs1_DX_bypass, Rs1_FD_bypass, Rs2_DX_bypass,
       Rs2_FD_bypass, Rt, Shamt;
  wire [16:0] Immediate;
  wire [26:0] Target;
  wire [31:0] alu_1_out_8, alu_out, alu_out_out, Immediate32, instruct, Instruct_DX, Instruct_FD,
       Instruct_MW, Instruct_XM, multdiv_res, multiplexer_3_out, multiplexer_7_out, multiplexer_11_out,
       multiplexer_12_out, multiplexer_13_out, multiplexer_14_out, multiplexer_15_out, multiplexer_18_out,
       multiplexer_19_out, multiplexer_20_out, multiplexer_24_out, n32_bit_compact_1_result, PC, PC_1,
       PC_add, PC_D, PC_M, PC_W, PC_W_1, PC_X, PC_X_1, PC_X_1_N, r1d, r1d_out, r1d_out_real, r2d, r2d_out,
       r2d_out_2, r2d_out_2_real, r2d_out_real, ram_1_data, register_32_2_output, RstatusWrite,
       Target_extend, To_PC, wdata, wdata_out;

  register_32 register_32_1 (.clk(rise), .\input (To_PC), .enable(not_stall), .\output (PC), .reset(reset));
  and and_1 (and_1_out, fall, Rwe);
  Multiplexer #(.width(5), .enable("false")) multiplexer_1 (
    .in0(multiplexer_2_out), .in1({5{1'b1}}), .out(multiplexer_1_out), .sel(JalC));
  Multiplexer #(.width(5), .enable("false")) multiplexer_2 (
    .in0(Rd_MW), .in1(5'b11110), .out(multiplexer_2_out), .sel(RstatusC));
  not not_1 (fall, rise);
  Clock clock_1 (.out(rise));
  register_32 register_32_2 (
    .clk(rise), .\input (n32_bit_compact_1_result), .enable(1'b1), .\output (register_32_2_output),
    .reset(reset));
  ROM #(.addrWidth(12), .dataWidth(32)) rom_1 (.addr(PC[11:0]), .data(instruct), .sel(fall));
  _32_bit_compact u_32_bit_compact_1 (
    .result(n32_bit_compact_1_result), .A(register_32_2_output), .B(32'h1), .sub(1'b0));  // open: ovf
  Multiplexer #(.width(32), .enable("false")) multiplexer_3 (
    .in0(wdata_out), .in1(PC_W_1), .out(multiplexer_3_out), .sel(JalC));
  or or_1 (or_1_out, BEXC, SETXC_D);
  Multiplexer #(.width(5), .enable("false")) multiplexer_4 (.in0(Rs), .in1(Rd), .out(multiplexer_4_out), .sel(RdC));
  Multiplexer #(.width(32), .enable("false")) multiplexer_5 (
    .in0(32'h1), .in1({32{1'b0}}), .out(PC_add), .sel(comparator_1_eq));
  Comparator #(.width(32)) comparator_1 (
    .a(32'h1), .b(n32_bit_compact_1_result), .eq(comparator_1_eq));  // open: gt, lt
  RegisterFile registerfile_1 (
    .WriteReg(multiplexer_1_out), .WriteData(multiplexer_3_out), .RegWriteEnable(Rwe), .clk(and_1_out),
    .reset(reset), .ReadData2(r2d), .ReadReg2(multiplexer_8_out), .ReadReg1(multiplexer_6_out),
    .ReadData1(r1d));
  Multiplexer #(.width(5), .enable("false")) multiplexer_6 (
    .in0(multiplexer_4_out), .in1(5'b11110), .out(multiplexer_6_out), .sel(or_1_out));
  Multiplexer #(.width(32), .enable("false")) multiplexer_7 (
    .in0(instruct), .in1({32{1'b0}}), .out(multiplexer_7_out), .sel(flush_signal));
  _32_bit_compact u_32_bit_compact_2 (.result(PC_1), .A(PC), .B(32'h1), .sub(1'b0));  // open: ovf
  _32_bit_compact u_32_bit_compact_3 (.result(PC_X_1), .A(PC_X), .B(32'h1), .sub(1'b0));  // open: ovf
  _32_bit_compact u_32_bit_compact_4 (.result(PC_W_1), .A(PC_W), .B(32'h1), .sub(1'b0));  // open: ovf
  Multiplexer #(.width(5), .enable("false")) multiplexer_8 (
    .in0(multiplexer_9_out), .in1({5{1'b0}}), .out(multiplexer_8_out), .sel(BEXC));
  Multiplexer #(.width(5), .enable("false")) multiplexer_9 (
    .in0(multiplexer_10_out), .in1(Rd), .out(multiplexer_9_out), .sel(SwC));
  Multiplexer #(.width(5), .enable("false")) multiplexer_10 (.in0(Rt), .in1(Rs), .out(multiplexer_10_out), .sel(RsC));
  F_D f_d_1 (
    .PC(PC), .Instruction(multiplexer_7_out), .clk(rise), .reset(reset), .Rt(Rt), .Rs(Rs), .Rd(Rd),
    .PC_out(PC_D), .Instruction_out(Instruct_FD), .RdC(RdC), .BEXC(BEXC), .RsC(RsC), .SwC(SwC),
    .SETXC(SETXC_D), .Rs2_FD(Rs2_FD_bypass), .Rs1_FD(Rs1_FD_bypass), .Opcode_FD(Opcode_FD), .enable(not_stall));
  Comparator #(.width(5)) comparator_2 (.a(Rs1_DX_bypass), .b(Rd_XM_bypass), .eq(comparator_2_eq));  // open: gt, lt
  Comparator #(.width(5)) comparator_3 (.a(Rs1_DX_bypass), .b(Rd_MW_bypass), .eq(comparator_3_eq));  // open: gt, lt
  Comparator #(.width(5)) comparator_4 (
    .a(Opcode_FD), .b(5'b00111), .gt(comparator_4_gt), .lt(comparator_4_lt));  // open: eq
  _32_bit_compact u_32_bit_compact_5 (.result(PC_X_1_N), .A(PC_X_1), .B(Immediate32), .sub(1'b0));  // open: ovf
  Comparator #(.width(5)) comparator_5 (.a(Rs1_FD_bypass), .b(Rd_DX_bypass), .eq(comparator_5_eq));  // open: gt, lt
  Comparator #(.width(5)) comparator_6 (.a(Rs2_FD_bypass), .b(Rd_DX_bypass), .eq(comparator_6_eq));  // open: gt, lt
  or or_2 (or_2_out, comparator_4_gt, comparator_4_lt);
  Multiplexer #(.width(32), .enable("false")) multiplexer_11 (
    .in0(r2d_out_real), .in1(Immediate32), .out(multiplexer_11_out), .sel(ALUinB));
  assign Immediate32 = {{15{Immediate[16]}}, Immediate};  // Bit_Extender bit_extender_1
  assign Target_extend = {{5{1'b0}}, Target};  // Bit_Extender bit_extender_2
  Multiplexer #(.width(32), .enable("false")) multiplexer_12 (
    .in0(r1d), .in1({32{1'b0}}), .out(multiplexer_12_out), .sel(flush_signal));
  Multiplexer #(.width(32), .enable("false")) multiplexer_13 (
    .in0(r2d), .in1({32{1'b0}}), .out(multiplexer_13_out), .sel(flush_signal));
  Multiplexer #(.width(32), .enable("false")) multiplexer_14 (
    .in0(Instruct_FD), .in1({32{1'b0}}), .out(multiplexer_14_out), .sel(flush_signal));
  and and_2 (and_2_out[1], SwC_XM_Not, comparator_2_eq);
  and and_3 (and_2_out[2], comparator_3_eq, SwC_MW_Not);
  Comparator #(.width(5)) comparator_7 (.a(Opcode_DX), .b(5'b01000), .eq(comparator_7_eq));  // open: gt, lt
  and and_4 (and_4_out, comparator_6_eq, or_2_out);
  ALU alu_1 (
    .InputData1(r1d_out_real), .ALUop(multiplexer_16_out), .InputData2(multiplexer_11_out),
    .out_8(alu_1_out_8), .shift(Shamt), .ovf(ovf), .BLT(BLT), .BNE(BNE));
  D_X d_x_1 (
    .clk(rise), .reset(reset), .r1d(multiplexer_12_out), .r2d(multiplexer_13_out), .PC(PC_D), .PC_out(PC_X),
    .ALUinB(ALUinB), .PConeNC(PConeNC), .PCTC(PCTC), .PCRdC(PCRdC), .BNEC(BNEC), .BLTC(BLTC),
    .ALUopAddC(ALUopAddC), .Instruction(multiplexer_14_out), .Instruction_out(Instruct_DX),
    .Immediate(Immediate), .Target(Target), .r1d_out(r1d_out), .r2d_out(r2d_out), .ALUop(ALUop),
    .Shamt(Shamt), .Rs1_DX(Rs1_DX_bypass), .Rs2_DX(Rs2_DX_bypass), .SETXC(SETXC_X), .BEXC_X(BEXC_X),
    .Opcode_DX(Opcode_DX), .Rd_DX_bypass(Rd_DX_bypass), .enable(not_stall_DX));
  or or_3 (or_3_out, comparator_5_eq, and_4_out);
  Multiplexer #(.width(32), .enable("false")) multiplexer_15 (
    .in0(PC_X), .in1(Target_extend), .out(multiplexer_15_out), .sel(PCTCR));
  Multiplexer #(.width(5), .enable("false")) multiplexer_16 (
    .in0(ALUop), .in1({5{1'b0}}), .out(multiplexer_16_out), .sel(ALUopAddC));
  multdiv_behavioral multdiv (
    .clk(rise), .mult_start(mult_start), .div_start(div_start), .A(r1d_out_real), .B(multiplexer_11_out),
    .mult_rdy(multdiv_mult_rdy), .out(multdiv_res), .div_rdy(multdiv_div_rdy));
  Multiplexer #(.select(4), .width(32), .enable("false")) multiplexer_17 (
    .in0(r1d_out), .in2(alu_out_out), .in4(wdata_out), .in6(alu_out_out), .out(r1d_out_real),
    .sel({1'b0, and_2_out, 1'b0}));  // open: in1, in3, in5, in7, in8, in9, in10, in11, in12, in13, in14, in15
  and and_5 (stall_lw_bypass, comparator_7_eq, or_3_out);
  Multiplexer #(.width(32), .enable("false")) multiplexer_18 (
    .in0(alu_1_out_8), .in1(multdiv_res), .out(multiplexer_18_out), .sel(data_resultRDY));
  or or_4 (data_resultRDY, multdiv_mult_rdy, multdiv_div_rdy);
  Multiplexer #(.width(32), .enable("false")) multiplexer_19 (
    .in0(multiplexer_15_out), .in1(PC_X_1_N), .out(multiplexer_19_out), .sel(PConeNCR));
  Comparator #(.width(5)) comparator_8 (.a(Rs2_DX_bypass), .b(Rd_XM_bypass), .eq(comparator_8_eq));  // open: gt, lt
  Comparator #(.width(5)) comparator_9 (.a(Rs2_DX_bypass), .b(Rd_MW_bypass), .eq(comparator_9_eq));  // open: gt, lt
  Multiplexer #(.width(32), .enable("false")) multiplexer_20 (
    .in0(multiplexer_19_out), .in1(r1d_out_real), .out(multiplexer_20_out), .sel(PCRdC));
  Multiplexer #(.width(32), .enable("false")) multiplexer_21 (
    .in0(multiplexer_18_out), .in1(Target_extend), .out(alu_out), .sel(SETXC_X));
  and and_6 (and_6_out[1], SwC_XM_Not, comparator_8_eq);
  and and_7 (and_6_out[2], comparator_9_eq, SwC_MW_Not);
  Multiplexer #(.width(32), .enable("false")) multiplexer_22 (
    .in0(PC_1), .in1(multiplexer_20_out), .out(To_PC), .sel(or_7_out));
  X_M x_m_1 (
    .clk(rise), .reset(reset), .PC(PC_X), .Instruction(Instruct_DX), .r2d(r2d_out_real), .PC_out(PC_M),
    .r2d_out(r2d_out_2), .alu_out(alu_out), .alu_out_out(alu_out_out), .DMwe(DMwe), .DMld(DMld),
    .MEMwrite(MEMwrite), .Rd_XM_bypass(Rd_XM_bypass), .SwC_XM(x_m_1_swc_xm), .ovf(ovf),
    .Instruction_out(Instruct_XM), .enable(not_stall_DX));
  not not_2 (SwC_XM_Not, x_m_1_swc_xm);
  Multiplexer #(.select(4), .width(32), .enable("false")) multiplexer_23 (
    .in0(r2d_out), .in2(alu_out_out), .in4(wdata_out), .in6(alu_out_out), .out(r2d_out_real),
    .sel({1'b0, and_6_out, 1'b0}));  // open: in1, in3, in5, in7, in8, in9, in10, in11, in12, in13, in14, in15
  or or_5 (or_5_out, mult_progress, div_progress);
  not not_3 (not_3_out, data_resultRDY);
  and and_8 (not_stall, not_stall_FD, not_stall_DX);
  Comparator #(.width(5)) comparator_10 (.a(ALUop), .b(5'b00110), .eq(comparator_10_eq));  // open: gt, lt
  Comparator #(.width(5)) comparator_11 (.a(ALUop), .b(5'b00111), .eq(comparator_11_eq));  // open: gt, lt
  buf or_6 (stall_FD, stall_lw_bypass);  // OR_Gate
  not not_4 (not_stall_FD, stall_FD);
  and and_9 (stall_DX, or_5_out, not_3_out);
  or or_7 (or_7_out, PCTCR, PConeNCR, PCRdC);
  D_Flip_Flop d_ff_1 (.clk(rise), .D(comparator_10_eq), .Q(d_ff_1_q), .reset(data_resultRDY));  // open: Qn, preset, en
  or or_8 (flush_signal, or_7_out, stall_lw_bypass);
  not not_5 (not_5_out, d_ff_1_q);
  D_Flip_Flop d_ff_2 (.clk(rise), .D(comparator_11_eq), .Q(d_ff_2_q), .reset(data_resultRDY));  // open: Qn, preset, en
  not not_6 (not_6_out, d_ff_2_q);
  not not_7 (not_7_out, data_resultRDY);
  Comparator #(.width(5)) comparator_12 (.a(Rd_MW_bypass), .b(Rd_XM_bypass), .eq(comparator_12_eq));  // open: gt, lt
  not not_8 (not_stall_DX, stall_DX);
  and and_10 (and_10_out, BLT, BLTC);
  and and_11 (and_11_out, BNEC, BNE);
  Multiplexer #(.width(32), .enable("false")) multiplexer_24 (
    .in0(alu_out_out), .in1(ram_1_data), .out(multiplexer_24_out), .sel(MEMwrite));
  RAM #(.addrWidth(12), .dataWidth(32), .bus("separate")) ram_1 (
    .addr(alu_out_out[11:0]), .din(r2d_out_2_real), .data(ram_1_data), .str(DMwe), .clk(rise), .ld(DMld));  // open: sel, clr
  and and_12 (mult_start, not_5_out, not_7_out, comparator_10_eq);
  and and_13 (div_start, not_6_out, not_7_out, comparator_11_eq);
  M_W m_w_1 (
    .clk(rise), .reset(reset), .PC(PC_M), .Instruction(Instruct_XM), .Rwe(Rwe), .JalC(JalC), .PC_out(PC_W),
    .RstatusC(RstatusC), .Instruction_out(Instruct_MW), .wdata(wdata), .wdata_out(wdata_out), .Rd_MW(Rd_MW),
    .Rd_MW_bypass(Rd_MW_bypass), .SwC_MW(m_w_1_swc_mw), .enable(not_stall_DX));
  and and_14 (and_14_out[1], SwC_MW_Not, SwC_MW_Not, comparator_12_eq);
  and and_15 (and_15_out, BNE, BEXC_X);
  Multiplexer #(.width(32), .enable("false")) multiplexer_25 (
    .in0(multiplexer_24_out), .in1(RstatusWrite), .out(wdata), .sel(1'b0));
  or or_9 (mult_progress, d_ff_1_q, mult_start);
  or or_10 (div_progress, d_ff_2_q, div_start);
  not not_9 (SwC_MW_Not, m_w_1_swc_mw);
  Multiplexer #(.select(2), .width(32), .enable("false")) multiplexer_26 (
    .in0(r2d_out_2), .in2(wdata_out), .out(r2d_out_2_real), .sel({and_14_out[1], 1'b0}));  // open: in1, in3
  or or_11 (PConeNCR, PConeNC, and_10_out, and_11_out);
  or or_12 (PCTCR, PCTC, and_15_out);

  // Notes on the sheet:
  //   PC
  //   PC
  //   $rstatus
  //   contents of rom_1 (hex, n*v repeats v):
  //   2842000a 38400000 40800000
  //   $r31
  //   $rstatus
endmodule

module RegisterFile (
  input  [31:0] WriteData,
  input  clk,
  input  [4:0] WriteReg,
  input  RegWriteEnable,
  input  reset,
  input  [4:0] ReadReg2,
  input  [4:0] ReadReg1,
  output [31:0] ReadData2,
  output [31:0] ReadData1
);

  wire decoder_1_out0, decoder_1_out1, decoder_1_out2, decoder_1_out3, decoder_1_out4, decoder_1_out5,
       decoder_1_out6, decoder_1_out7, decoder_1_out8, decoder_1_out9, decoder_1_out10, decoder_1_out11,
       decoder_1_out12, decoder_1_out13, decoder_1_out14, decoder_1_out15, decoder_1_out16, decoder_1_out17,
       decoder_1_out18, decoder_1_out19, decoder_1_out20, decoder_1_out21, decoder_1_out22, decoder_1_out23,
       decoder_1_out24, decoder_1_out25, decoder_1_out26, decoder_1_out27, decoder_1_out28, decoder_1_out29,
       decoder_1_out30, decoder_1_out31, decoder_2_out0, decoder_2_out1, decoder_2_out2, decoder_2_out3,
       decoder_2_out4, decoder_2_out5, decoder_2_out6, decoder_2_out7, decoder_2_out8, decoder_2_out9,
       decoder_2_out10, decoder_2_out11, decoder_2_out12, decoder_2_out13, decoder_2_out14, decoder_2_out15,
       decoder_2_out16, decoder_2_out17, decoder_2_out18, decoder_2_out19, decoder_2_out20, decoder_2_out21,
       decoder_2_out22, decoder_2_out23, decoder_2_out24, decoder_2_out25, decoder_2_out26, decoder_2_out27,
       decoder_2_out28, decoder_2_out29, decoder_2_out30, decoder_2_out31, decoder_3_out0, decoder_3_out1,
       decoder_3_out2, decoder_3_out3, decoder_3_out4, decoder_3_out5, decoder_3_out6, decoder_3_out7,
       decoder_3_out8, decoder_3_out9, decoder_3_out10, decoder_3_out11, decoder_3_out12, decoder_3_out13,
       decoder_3_out14, decoder_3_out15, decoder_3_out16, decoder_3_out17, decoder_3_out18, decoder_3_out19,
       decoder_3_out20, decoder_3_out21, decoder_3_out22, decoder_3_out23, decoder_3_out24, decoder_3_out25,
       decoder_3_out26, decoder_3_out27, decoder_3_out28, decoder_3_out29, decoder_3_out30, decoder_3_out31,
       enab, not_1_out;
  wire [31:0] _0, _1, _2, _3, _4, _5, _6, _7, _8, _9, _10, _11, _12, _13, _14, _15, _16, _17, _18, _19, _20,
       _21, _22, _23, _24, _25, _26, _27, _28, _29, _30, _31;

  assign ReadData2 = decoder_2_out0 ? _0 : 32'bz;  // Controlled_Buffer controlled_buffer_1
  assign ReadData1 = decoder_3_out0 ? _0 : 32'bz;  // Controlled_Buffer controlled_buffer_2
  Decoder #(.select(5), .enable("false")) decoder_1 (
    .out0(decoder_1_out0), .out1(decoder_1_out1), .out2(decoder_1_out2), .out3(decoder_1_out3),
    .out4(decoder_1_out4), .out5(decoder_1_out5), .out6(decoder_1_out6), .out7(decoder_1_out7),
    .out8(decoder_1_out8), .out9(decoder_1_out9), .out10(decoder_1_out10), .out11(decoder_1_out11),
    .out12(decoder_1_out12), .out13(decoder_1_out13), .out14(decoder_1_out14), .out15(decoder_1_out15),
    .out16(decoder_1_out16), .out17(decoder_1_out17), .out18(decoder_1_out18), .out19(decoder_1_out19),
    .out20(decoder_1_out20), .out21(decoder_1_out21), .out22(decoder_1_out22), .out23(decoder_1_out23),
    .out24(decoder_1_out24), .out25(decoder_1_out25), .out26(decoder_1_out26), .out27(decoder_1_out27),
    .out28(decoder_1_out28), .out29(decoder_1_out29), .out30(decoder_1_out30), .out31(decoder_1_out31),
    .sel(WriteReg));
  assign ReadData2 = decoder_2_out1 ? _1 : 32'bz;  // Controlled_Buffer controlled_buffer_3
  assign ReadData1 = decoder_3_out1 ? _1 : 32'bz;  // Controlled_Buffer controlled_buffer_4
  register_32 register_32_1 (.clk(clk), .\input (WriteData), .enable(1'b0), .\output (_0), .reset(reset));
  register_32 register_32_2 (.clk(clk), .\input (WriteData), .enable(decoder_1_out1), .\output (_1), .reset(reset));
  register_32 register_32_3 (.clk(clk), .\input (WriteData), .enable(decoder_1_out2), .\output (_2), .reset(reset));
  register_32 register_32_4 (.clk(clk), .\input (WriteData), .enable(decoder_1_out3), .\output (_3), .reset(reset));
  register_32 register_32_5 (.clk(clk), .\input (WriteData), .enable(decoder_1_out4), .\output (_4), .reset(reset));
  register_32 register_32_6 (.clk(clk), .\input (WriteData), .enable(decoder_1_out5), .\output (_5), .reset(reset));
  register_32 register_32_7 (.clk(clk), .\input (WriteData), .enable(decoder_1_out6), .\output (_6), .reset(reset));
  register_32 register_32_8 (.clk(clk), .\input (WriteData), .enable(decoder_1_out7), .\output (_7), .reset(reset));
  assign ReadData2 = decoder_2_out3 ? _3 : 32'bz;  // Controlled_Buffer controlled_buffer_5
  assign ReadData2 = decoder_2_out2 ? _2 : 32'bz;  // Controlled_Buffer controlled_buffer_6
  assign ReadData1 = decoder_3_out3 ? _3 : 32'bz;  // Controlled_Buffer controlled_buffer_7
  assign ReadData1 = decoder_3_out2 ? _2 : 32'bz;  // Controlled_Buffer controlled_buffer_8
  assign ReadData2 = decoder_2_out4 ? _4 : 32'bz;  // Controlled_Buffer controlled_buffer_9
  assign ReadData1 = decoder_3_out4 ? _4 : 32'bz;  // Controlled_Buffer controlled_buffer_10
  assign ReadData1 = decoder_3_out5 ? _5 : 32'bz;  // Controlled_Buffer controlled_buffer_11
  assign ReadData2 = decoder_2_out5 ? _5 : 32'bz;  // Controlled_Buffer controlled_buffer_12
  assign ReadData2 = decoder_2_out6 ? _6 : 32'bz;  // Controlled_Buffer controlled_buffer_13
  assign ReadData1 = decoder_3_out6 ? _6 : 32'bz;  // Controlled_Buffer controlled_buffer_14
  register_32 register_32_9 (.clk(clk), .\input (WriteData), .enable(decoder_1_out8), .\output (_8), .reset(reset));
  register_32 register_32_10 (.clk(clk), .\input (WriteData), .enable(decoder_1_out9), .\output (_9), .reset(reset));
  register_32 register_32_11 (.clk(clk), .\input (WriteData), .enable(decoder_1_out10), .\output (_10), .reset(reset));
  register_32 register_32_12 (.clk(clk), .\input (WriteData), .enable(decoder_1_out11), .\output (_11), .reset(reset));
  register_32 register_32_13 (.clk(clk), .\input (WriteData), .enable(decoder_1_out12), .\output (_12), .reset(reset));
  register_32 register_32_14 (.clk(clk), .\input (WriteData), .enable(decoder_1_out13), .\output (_13), .reset(reset));
  register_32 register_32_15 (.clk(clk), .\input (WriteData), .enable(decoder_1_out14), .\output (_14), .reset(reset));
  register_32 register_32_16 (.clk(clk), .\input (WriteData), .enable(decoder_1_out15), .\output (_15), .reset(reset));
  assign ReadData2 = decoder_2_out8 ? _8 : 32'bz;  // Controlled_Buffer controlled_buffer_15
  assign ReadData2 = decoder_2_out7 ? _7 : 32'bz;  // Controlled_Buffer controlled_buffer_16
  assign ReadData1 = decoder_3_out7 ? _7 : 32'bz;  // Controlled_Buffer controlled_buffer_17
  assign ReadData1 = decoder_3_out8 ? _8 : 32'bz;  // Controlled_Buffer controlled_buffer_18
  assign ReadData2 = decoder_2_out9 ? _9 : 32'bz;  // Controlled_Buffer controlled_buffer_19
  assign ReadData1 = decoder_3_out9 ? _9 : 32'bz;  // Controlled_Buffer controlled_buffer_20
  assign ReadData2 = decoder_2_out10 ? _10 : 32'bz;  // Controlled_Buffer controlled_buffer_21
  assign ReadData2 = decoder_2_out11 ? _11 : 32'bz;  // Controlled_Buffer controlled_buffer_22
  assign ReadData1 = decoder_3_out10 ? _10 : 32'bz;  // Controlled_Buffer controlled_buffer_23
  assign ReadData1 = decoder_3_out11 ? _11 : 32'bz;  // Controlled_Buffer controlled_buffer_24
  assign ReadData2 = decoder_2_out12 ? _12 : 32'bz;  // Controlled_Buffer controlled_buffer_25
  assign ReadData1 = decoder_3_out12 ? _12 : 32'bz;  // Controlled_Buffer controlled_buffer_26
  assign ReadData1 = decoder_3_out13 ? _13 : 32'bz;  // Controlled_Buffer controlled_buffer_27
  register_32 register_32_17 (.clk(clk), .\input (WriteData), .enable(decoder_1_out16), .\output (_16), .reset(reset));
  register_32 register_32_18 (.clk(clk), .\input (WriteData), .enable(decoder_1_out17), .\output (_17), .reset(reset));
  register_32 register_32_19 (.clk(clk), .\input (WriteData), .enable(decoder_1_out18), .\output (_18), .reset(reset));
  register_32 register_32_20 (.clk(clk), .\input (WriteData), .enable(decoder_1_out19), .\output (_19), .reset(reset));
  register_32 register_32_21 (.clk(clk), .\input (WriteData), .enable(decoder_1_out20), .\output (_20), .reset(reset));
  register_32 register_32_22 (.clk(clk), .\input (WriteData), .enable(decoder_1_out21), .\output (_21), .reset(reset));
  register_32 register_32_23 (.clk(clk), .\input (WriteData), .enable(decoder_1_out22), .\output (_22), .reset(reset));
  register_32 register_32_24 (.clk(clk), .\input (WriteData), .enable(decoder_1_out23), .\output (_23), .reset(reset));
  assign ReadData2 = decoder_2_out14 ? _14 : 32'bz;  // Controlled_Buffer controlled_buffer_28
  assign ReadData2 = decoder_2_out13 ? _13 : 32'bz;  // Controlled_Buffer controlled_buffer_29
  Decoder #(.select(5), .enable("false")) decoder_2 (
    .out0(decoder_2_out0), .out1(decoder_2_out1), .out2(decoder_2_out2), .out3(decoder_2_out3),
    .out4(decoder_2_out4), .out5(decoder_2_out5), .out6(decoder_2_out6), .out7(decoder_2_out7),
    .out8(decoder_2_out8), .out9(decoder_2_out9), .out10(decoder_2_out10), .out11(decoder_2_out11),
    .out12(decoder_2_out12), .out13(decoder_2_out13), .out14(decoder_2_out14), .out15(decoder_2_out15),
    .out16(decoder_2_out16), .out17(decoder_2_out17), .out18(decoder_2_out18), .out19(decoder_2_out19),
    .out20(decoder_2_out20), .out21(decoder_2_out21), .out22(decoder_2_out22), .out23(decoder_2_out23),
    .out24(decoder_2_out24), .out25(decoder_2_out25), .out26(decoder_2_out26), .out27(decoder_2_out27),
    .out28(decoder_2_out28), .out29(decoder_2_out29), .out30(decoder_2_out30), .out31(decoder_2_out31),
    .sel(ReadReg2));
  assign ReadData1 = decoder_3_out14 ? _14 : 32'bz;  // Controlled_Buffer controlled_buffer_30
  Decoder #(.select(5), .enable("false")) decoder_3 (
    .out0(decoder_3_out0), .out1(decoder_3_out1), .out2(decoder_3_out2), .out3(decoder_3_out3),
    .out4(decoder_3_out4), .out5(decoder_3_out5), .out6(decoder_3_out6), .out7(decoder_3_out7),
    .out8(decoder_3_out8), .out9(decoder_3_out9), .out10(decoder_3_out10), .out11(decoder_3_out11),
    .out12(decoder_3_out12), .out13(decoder_3_out13), .out14(decoder_3_out14), .out15(decoder_3_out15),
    .out16(decoder_3_out16), .out17(decoder_3_out17), .out18(decoder_3_out18), .out19(decoder_3_out19),
    .out20(decoder_3_out20), .out21(decoder_3_out21), .out22(decoder_3_out22), .out23(decoder_3_out23),
    .out24(decoder_3_out24), .out25(decoder_3_out25), .out26(decoder_3_out26), .out27(decoder_3_out27),
    .out28(decoder_3_out28), .out29(decoder_3_out29), .out30(decoder_3_out30), .out31(decoder_3_out31),
    .sel(ReadReg1));
  assign ReadData2 = decoder_2_out15 ? _15 : 32'bz;  // Controlled_Buffer controlled_buffer_31
  assign ReadData1 = decoder_3_out15 ? _15 : 32'bz;  // Controlled_Buffer controlled_buffer_32
  assign ReadData2 = decoder_2_out16 ? _16 : 32'bz;  // Controlled_Buffer controlled_buffer_33
  assign ReadData1 = decoder_3_out16 ? _16 : 32'bz;  // Controlled_Buffer controlled_buffer_34
  register_32 register_32_25 (.clk(clk), .\input (WriteData), .enable(decoder_1_out24), .\output (_24), .reset(reset));
  register_32 register_32_26 (.clk(clk), .\input (WriteData), .enable(decoder_1_out25), .\output (_25), .reset(reset));
  register_32 register_32_27 (.clk(clk), .\input (WriteData), .enable(decoder_1_out26), .\output (_26), .reset(reset));
  register_32 register_32_28 (.clk(clk), .\input (WriteData), .enable(decoder_1_out27), .\output (_27), .reset(reset));
  register_32 register_32_29 (.clk(clk), .\input (WriteData), .enable(decoder_1_out28), .\output (_28), .reset(reset));
  register_32 register_32_30 (.clk(clk), .\input (WriteData), .enable(decoder_1_out29), .\output (_29), .reset(reset));
  register_32 register_32_31 (.clk(clk), .\input (WriteData), .enable(decoder_1_out30), .\output (_30), .reset(reset));
  register_32 register_32_32 (.clk(clk), .\input (WriteData), .enable(decoder_1_out31), .\output (_31), .reset(reset));
  assign ReadData2 = decoder_2_out18 ? _18 : 32'bz;  // Controlled_Buffer controlled_buffer_35
  assign ReadData2 = decoder_2_out17 ? _17 : 32'bz;  // Controlled_Buffer controlled_buffer_36
  assign ReadData1 = decoder_3_out17 ? _17 : 32'bz;  // Controlled_Buffer controlled_buffer_37
  assign ReadData1 = decoder_3_out18 ? _18 : 32'bz;  // Controlled_Buffer controlled_buffer_38
  assign ReadData2 = decoder_2_out19 ? _19 : 32'bz;  // Controlled_Buffer controlled_buffer_39
  assign ReadData1 = decoder_3_out19 ? _19 : 32'bz;  // Controlled_Buffer controlled_buffer_40
  assign ReadData1 = decoder_3_out20 ? _20 : 32'bz;  // Controlled_Buffer controlled_buffer_41
  assign ReadData2 = decoder_2_out20 ? _20 : 32'bz;  // Controlled_Buffer controlled_buffer_42
  assign ReadData2 = decoder_2_out21 ? _21 : 32'bz;  // Controlled_Buffer controlled_buffer_43
  assign ReadData1 = decoder_3_out21 ? _21 : 32'bz;  // Controlled_Buffer controlled_buffer_44
  not not_1 (not_1_out, clk);
  assign ReadData2 = decoder_2_out23 ? _23 : 32'bz;  // Controlled_Buffer controlled_buffer_45
  assign ReadData2 = decoder_2_out22 ? _22 : 32'bz;  // Controlled_Buffer controlled_buffer_46
  assign ReadData1 = decoder_3_out22 ? _22 : 32'bz;  // Controlled_Buffer controlled_buffer_47
  assign ReadData1 = decoder_3_out23 ? _23 : 32'bz;  // Controlled_Buffer controlled_buffer_48
  and and_1 (enab, RegWriteEnable, not_1_out);
  assign ReadData2 = decoder_2_out24 ? _24 : 32'bz;  // Controlled_Buffer controlled_buffer_49
  assign ReadData1 = decoder_3_out24 ? _24 : 32'bz;  // Controlled_Buffer controlled_buffer_50
  assign ReadData2 = decoder_2_out25 ? _25 : 32'bz;  // Controlled_Buffer controlled_buffer_51
  assign ReadData2 = decoder_2_out26 ? _26 : 32'bz;  // Controlled_Buffer controlled_buffer_52
  assign ReadData1 = decoder_3_out25 ? _25 : 32'bz;  // Controlled_Buffer controlled_buffer_53
  assign ReadData1 = decoder_3_out26 ? _26 : 32'bz;  // Controlled_Buffer controlled_buffer_54
  assign ReadData2 = decoder_2_out27 ? _27 : 32'bz;  // Controlled_Buffer controlled_buffer_55
  assign ReadData1 = decoder_3_out28 ? _28 : 32'bz;  // Controlled_Buffer controlled_buffer_56
  assign ReadData1 = decoder_3_out27 ? _27 : 32'bz;  // Controlled_Buffer controlled_buffer_57
  assign ReadData2 = decoder_2_out28 ? _28 : 32'bz;  // Controlled_Buffer controlled_buffer_58
  assign ReadData2 = decoder_2_out29 ? _29 : 32'bz;  // Controlled_Buffer controlled_buffer_59
  assign ReadData1 = decoder_3_out29 ? _29 : 32'bz;  // Controlled_Buffer controlled_buffer_60
  assign ReadData2 = decoder_2_out31 ? _31 : 32'bz;  // Controlled_Buffer controlled_buffer_61
  assign ReadData2 = decoder_2_out30 ? _30 : 32'bz;  // Controlled_Buffer controlled_buffer_62
  assign ReadData1 = decoder_3_out31 ? _31 : 32'bz;  // Controlled_Buffer controlled_buffer_63
  assign ReadData1 = decoder_3_out30 ? _30 : 32'bz;  // Controlled_Buffer controlled_buffer_64

  // Other names for the same wires on the sheet: data[31:0] = WriteData
endmodule

module register_32 (
  input  enable,
  input  reset,
  input  clk,
  input  [31:0] \input ,
  output [31:0] \output 
);

  wire enable_t, not_1_out;

  not not_1 (not_1_out, clk);
  and and_1 (enable_t, not_1_out, enable);
  D_Flip_Flop d_ff_1 (.clk(clk), .D(\input [0]), .Q(\output [0]), .en(enable_t), .reset(reset));  // open: Qn, preset
  D_Flip_Flop d_ff_2 (.clk(clk), .D(\input [1]), .Q(\output [1]), .en(enable_t), .reset(reset));  // open: Qn, preset
  D_Flip_Flop d_ff_3 (.clk(clk), .D(\input [2]), .Q(\output [2]), .en(enable_t), .reset(reset));  // open: Qn, preset
  D_Flip_Flop d_ff_4 (.clk(clk), .D(\input [3]), .Q(\output [3]), .en(enable_t), .reset(reset));  // open: Qn, preset
  D_Flip_Flop d_ff_5 (.clk(clk), .D(\input [4]), .Q(\output [4]), .en(enable_t), .reset(reset));  // open: Qn, preset
  D_Flip_Flop d_ff_6 (.clk(clk), .D(\input [5]), .Q(\output [5]), .en(enable_t), .reset(reset));  // open: Qn, preset
  D_Flip_Flop d_ff_7 (.clk(clk), .D(\input [6]), .Q(\output [6]), .en(enable_t), .reset(reset));  // open: Qn, preset
  D_Flip_Flop d_ff_8 (.clk(clk), .D(\input [7]), .Q(\output [7]), .en(enable_t), .reset(reset));  // open: Qn, preset
  D_Flip_Flop d_ff_9 (.clk(clk), .D(\input [16]), .Q(\output [16]), .en(enable_t), .reset(reset));  // open: Qn, preset
  D_Flip_Flop d_ff_10 (.clk(clk), .D(\input [17]), .Q(\output [17]), .en(enable_t), .reset(reset));  // open: Qn, preset
  D_Flip_Flop d_ff_11 (.clk(clk), .D(\input [18]), .Q(\output [18]), .en(enable_t), .reset(reset));  // open: Qn, preset
  D_Flip_Flop d_ff_12 (.clk(clk), .D(\input [19]), .Q(\output [19]), .en(enable_t), .reset(reset));  // open: Qn, preset
  D_Flip_Flop d_ff_13 (.clk(clk), .D(\input [20]), .Q(\output [20]), .en(enable_t), .reset(reset));  // open: Qn, preset
  D_Flip_Flop d_ff_14 (.clk(clk), .D(\input [21]), .Q(\output [21]), .en(enable_t), .reset(reset));  // open: Qn, preset
  D_Flip_Flop d_ff_15 (.clk(clk), .D(\input [22]), .Q(\output [22]), .en(enable_t), .reset(reset));  // open: Qn, preset
  D_Flip_Flop d_ff_16 (.clk(clk), .D(\input [23]), .Q(\output [23]), .en(enable_t), .reset(reset));  // open: Qn, preset
  D_Flip_Flop d_ff_17 (.clk(clk), .D(\input [8]), .Q(\output [8]), .en(enable_t), .reset(reset));  // open: Qn, preset
  D_Flip_Flop d_ff_18 (.clk(clk), .D(\input [9]), .Q(\output [9]), .en(enable_t), .reset(reset));  // open: Qn, preset
  D_Flip_Flop d_ff_19 (.clk(clk), .D(\input [10]), .Q(\output [10]), .en(enable_t), .reset(reset));  // open: Qn, preset
  D_Flip_Flop d_ff_20 (.clk(clk), .D(\input [11]), .Q(\output [11]), .en(enable_t), .reset(reset));  // open: Qn, preset
  D_Flip_Flop d_ff_21 (.clk(clk), .D(\input [12]), .Q(\output [12]), .en(enable_t), .reset(reset));  // open: Qn, preset
  D_Flip_Flop d_ff_22 (.clk(clk), .D(\input [13]), .Q(\output [13]), .en(enable_t), .reset(reset));  // open: Qn, preset
  D_Flip_Flop d_ff_23 (.clk(clk), .D(\input [14]), .Q(\output [14]), .en(enable_t), .reset(reset));  // open: Qn, preset
  D_Flip_Flop d_ff_24 (.clk(clk), .D(\input [15]), .Q(\output [15]), .en(enable_t), .reset(reset));  // open: Qn, preset
  D_Flip_Flop d_ff_25 (.clk(clk), .D(\input [24]), .Q(\output [24]), .en(enable_t), .reset(reset));  // open: Qn, preset
  D_Flip_Flop d_ff_26 (.clk(clk), .D(\input [25]), .Q(\output [25]), .en(enable_t), .reset(reset));  // open: Qn, preset
  D_Flip_Flop d_ff_27 (.clk(clk), .D(\input [26]), .Q(\output [26]), .en(enable_t), .reset(reset));  // open: Qn, preset
  D_Flip_Flop d_ff_28 (.clk(clk), .D(\input [27]), .Q(\output [27]), .en(enable_t), .reset(reset));  // open: Qn, preset
  D_Flip_Flop d_ff_29 (.clk(clk), .D(\input [28]), .Q(\output [28]), .en(enable_t), .reset(reset));  // open: Qn, preset
  D_Flip_Flop d_ff_30 (.clk(clk), .D(\input [29]), .Q(\output [29]), .en(enable_t), .reset(reset));  // open: Qn, preset
  D_Flip_Flop d_ff_31 (.clk(clk), .D(\input [30]), .Q(\output [30]), .en(enable_t), .reset(reset));  // open: Qn, preset
  D_Flip_Flop d_ff_32 (.clk(clk), .D(\input [31]), .Q(\output [31]), .en(enable_t), .reset(reset));  // open: Qn, preset

  // Other names for the same wires on the sheet: first[7:0] = \input [7:0]; second[7:0] = \input [15:8];
  //   third[7:0] = \input [23:16]; fourth[7:0] = \input [31:24]
endmodule

module decoder_3to8 (
  input  [2:0] \input ,
  output out0,
  output out1,
  output out2,
  output out3,
  output out4,
  output out5,
  output out6,
  output out7
);

  wire not_1_out, not_2_out, not_3_out;

  not not_1 (not_1_out, \input [0]);
  not not_2 (not_2_out, \input [1]);
  not not_3 (not_3_out, \input [2]);
  and and_1 (out0, not_1_out, not_2_out, not_3_out);
  and and_2 (out1, \input [0], not_2_out, not_3_out);
  and and_3 (out2, not_1_out, \input [1], not_3_out);
  and and_4 (out3, \input [0], \input [1], not_3_out);
  and and_5 (out4, \input [2], not_1_out, not_2_out);
  and and_6 (out5, \input [2], not_2_out, \input [0]);
  and and_7 (out6, not_1_out, \input [1], \input [2]);
  and and_8 (out7, \input [0], \input [1], \input [2]);
endmodule

module ALU (
  input  [4:0] shift,
  input  [4:0] ALUop,
  input  [31:0] InputData1,
  input  [31:0] InputData2,
  output ovf,
  output BLT,
  output BNE,
  output [31:0] out_8
);

  wire comparator_1_eq, n32_bit_compact_1_ovf, n32_bit_compact_2_ovf;
  wire [31:0] and_1_out, divider_1_out, multiplier_1_out, n32_bit_compact_1_result, n32_bit_compact_2_result,
       or_1_out, shifter_1_out, shifter_2_out;

  Shifter #(.width(32)) shifter_1 (.in(InputData1), .\dist (shift), .out(shifter_1_out));
  Shifter #(.width(32), .shift("ar")) shifter_2 (.in(InputData1), .\dist (shift), .out(shifter_2_out));
  _32_bit_compact u_32_bit_compact_1 (
    .result(n32_bit_compact_1_result), .A(InputData1), .B(InputData2), .ovf(n32_bit_compact_1_ovf), .sub(1'b0));
  _32_bit_compact u_32_bit_compact_2 (
    .result(n32_bit_compact_2_result), .A(InputData1), .B(InputData2), .ovf(n32_bit_compact_2_ovf), .sub(1'b1));
  assign and_1_out = InputData1 & InputData2;  // AND_Gate and_1, 32 bits wide
  assign or_1_out = InputData1 | InputData2;  // OR_Gate or_1, 32 bits wide
  or or_2 (ovf, n32_bit_compact_2_ovf, n32_bit_compact_1_ovf);
  Multiplier #(.width(32)) multiplier_1 (.a(InputData1), .b(InputData2), .out(multiplier_1_out));  // open: cin, cout
  Divider #(.width(32)) divider_1 (.a(InputData1), .b(InputData2), .out(divider_1_out));  // open: upper, rem
  Multiplexer #(.select(5), .width(32), .enable("false")) multiplexer_1 (
    .in0(n32_bit_compact_1_result), .in1(n32_bit_compact_2_result), .in2(and_1_out), .in3(or_1_out),
    .in4(shifter_1_out), .in5(shifter_2_out), .in6(multiplier_1_out), .in7(divider_1_out), .out(out_8),
    .sel(ALUop));  // open: in8, in9, in10, in11, in12, in13, in14, in15, in16, in17, in18, in19, in20, in21, in22, in23, in24, in25, in26, in27, in28, in29, in30, in31
  Comparator #(.width(32)) comparator_1 (.a(InputData1), .b(InputData2), .eq(comparator_1_eq), .lt(BLT));  // open: gt
  not not_1 (BNE, comparator_1_eq);

  // Other names for the same wires on the sheet: A[31:0] = InputData1; B[31:0] = InputData2
endmodule

module one_bit_add (
  input  cin,
  input  a,
  input  b,
  output cout,
  output sum
);

  wire and_1_out, and_2_out, xor_1_out;

  or or_1 (cout, and_1_out, and_2_out);
  xor xor_1 (xor_1_out, a, b);
  and and_1 (and_1_out, a, b);
  and and_2 (and_2_out, xor_1_out, cin);
  xor xor_2 (sum, cin, xor_1_out);
endmodule

module _16_bit_add (
  input  add_sub,
  input  a15,
  input  b15,
  input  a14,
  input  b14,
  input  a13,
  input  b13,
  input  a12,
  input  b12,
  input  a11,
  input  b11,
  input  a10,
  input  b10,
  input  a9,
  input  b9,
  input  a8,
  input  b8,
  input  a7,
  input  b7,
  input  a6,
  input  b6,
  input  a5,
  input  b5,
  input  a4,
  input  b4,
  input  a3,
  input  b3,
  input  a2,
  input  b2,
  input  a1,
  input  b1,
  input  a0,
  input  b0,
  output ovf,
  output s15,
  output s14,
  output s13,
  output s12,
  output s11,
  output s10,
  output s9,
  output s8,
  output cout,
  output s7,
  output s6,
  output s5,
  output s4,
  output s3,
  output s2,
  output s1,
  output s0
);

  wire one_bit_add_2_cout, one_bit_add_3_cout, one_bit_add_4_cout, one_bit_add_5_cout, one_bit_add_6_cout,
       one_bit_add_7_cout, one_bit_add_8_cout, one_bit_add_9_cout, one_bit_add_10_cout, one_bit_add_11_cout,
       one_bit_add_12_cout, one_bit_add_13_cout, one_bit_add_14_cout, one_bit_add_15_cout,
       one_bit_add_16_cout, xor_2_out, xor_3_out, xor_4_out, xor_5_out, xor_6_out, xor_7_out, xor_8_out,
       xor_9_out, xor_10_out, xor_11_out, xor_12_out, xor_13_out, xor_14_out, xor_15_out, xor_16_out,
       xor_17_out;

  xor xor_1 (ovf, cout, one_bit_add_3_cout);
  one_bit_add one_bit_add_1 (.a(a15), .b(xor_2_out), .cout(cout), .cin(one_bit_add_3_cout), .sum(s15));
  xor xor_2 (xor_2_out, add_sub, b15);
  one_bit_add one_bit_add_2 (.a(a7), .b(xor_3_out), .cout(one_bit_add_2_cout), .cin(one_bit_add_4_cout), .sum(s7));
  xor xor_3 (xor_3_out, add_sub, b7);
  one_bit_add one_bit_add_3 (.a(a14), .b(xor_4_out), .cout(one_bit_add_3_cout), .cin(one_bit_add_5_cout), .sum(s14));
  xor xor_4 (xor_4_out, add_sub, b14);
  one_bit_add one_bit_add_4 (.a(a6), .b(xor_5_out), .cout(one_bit_add_4_cout), .cin(one_bit_add_6_cout), .sum(s6));
  xor xor_5 (xor_5_out, add_sub, b6);
  one_bit_add one_bit_add_5 (.a(a13), .b(xor_6_out), .cout(one_bit_add_5_cout), .cin(one_bit_add_7_cout), .sum(s13));
  xor xor_6 (xor_6_out, add_sub, b13);
  one_bit_add one_bit_add_6 (.a(a5), .b(xor_7_out), .cout(one_bit_add_6_cout), .cin(one_bit_add_8_cout), .sum(s5));
  xor xor_7 (xor_7_out, add_sub, b5);
  one_bit_add one_bit_add_7 (.a(a12), .b(xor_8_out), .cout(one_bit_add_7_cout), .cin(one_bit_add_9_cout), .sum(s12));
  xor xor_8 (xor_8_out, add_sub, b12);
  one_bit_add one_bit_add_8 (.a(a4), .b(xor_9_out), .cout(one_bit_add_8_cout), .cin(one_bit_add_10_cout), .sum(s4));
  one_bit_add one_bit_add_9 (.a(a11), .b(xor_10_out), .cout(one_bit_add_9_cout), .cin(one_bit_add_11_cout), .sum(s11));
  one_bit_add one_bit_add_10 (.a(a3), .b(xor_11_out), .cout(one_bit_add_10_cout), .cin(one_bit_add_12_cout), .sum(s3));
  xor xor_9 (xor_9_out, add_sub, b4);
  one_bit_add one_bit_add_11 (
    .a(a10), .b(xor_12_out), .cout(one_bit_add_11_cout), .cin(one_bit_add_13_cout), .sum(s10));
  xor xor_10 (xor_10_out, add_sub, b11);
  xor xor_11 (xor_11_out, add_sub, b3);
  xor xor_12 (xor_12_out, add_sub, b10);
  one_bit_add one_bit_add_12 (.a(a2), .b(xor_13_out), .cout(one_bit_add_12_cout), .cin(one_bit_add_14_cout), .sum(s2));
  xor xor_13 (xor_13_out, add_sub, b2);
  one_bit_add one_bit_add_13 (.a(a9), .b(xor_14_out), .cout(one_bit_add_13_cout), .cin(one_bit_add_15_cout), .sum(s9));
  xor xor_14 (xor_14_out, add_sub, b9);
  one_bit_add one_bit_add_14 (.a(a1), .b(xor_15_out), .cout(one_bit_add_14_cout), .cin(one_bit_add_16_cout), .sum(s1));
  xor xor_15 (xor_15_out, add_sub, b1);
  one_bit_add one_bit_add_15 (.a(a8), .b(xor_16_out), .cout(one_bit_add_15_cout), .cin(one_bit_add_2_cout), .sum(s8));
  xor xor_16 (xor_16_out, add_sub, b8);
  one_bit_add one_bit_add_16 (.a(a0), .b(xor_17_out), .cout(one_bit_add_16_cout), .cin(add_sub), .sum(s0));
  xor xor_17 (xor_17_out, add_sub, b0);
endmodule

// add
module _16_bit_compact (
  input  [15:0] A,
  input  [15:0] B,
  input  sub,
  output ovf,
  output [15:0] result
);

  _16_bit_add u_16_bit_add_1 (
    .add_sub(sub), .ovf(ovf), .s7(result[7]), .s15(result[15]), .s14(result[14]), .s6(result[6]),
    .s13(result[13]), .s5(result[5]), .s12(result[12]), .s4(result[4]), .s11(result[11]), .s3(result[3]),
    .s10(result[10]), .s2(result[2]), .s9(result[9]), .s1(result[1]), .s8(result[8]), .s0(result[0]),
    .a15(A[15]), .a7(A[7]), .b15(B[15]), .b7(B[7]), .a14(A[14]), .a6(A[6]), .b14(B[14]), .b6(B[6]),
    .a13(A[13]), .a5(A[5]), .b13(B[13]), .b5(B[5]), .a12(A[12]), .a4(A[4]), .b12(B[12]), .b4(B[4]),
    .a11(A[11]), .a3(A[3]), .b11(B[11]), .b3(B[3]), .a10(A[10]), .a2(A[2]), .b10(B[10]), .b2(B[2]),
    .a9(A[9]), .a1(A[1]), .b9(B[9]), .b1(B[1]), .a8(A[8]), .a0(A[0]), .b8(B[8]), .b0(B[0]));  // open: cout
endmodule

// shftr
module shift_16_3_bit (
  input  [15:0] \input ,
  input  [2:0] shift,
  output [15:0] \output 
);

  wire multiplexer_1_out, multiplexer_2_out, multiplexer_3_out, multiplexer_4_out, multiplexer_5_out,
       multiplexer_6_out, multiplexer_7_out, multiplexer_8_out, multiplexer_9_out, multiplexer_10_out,
       multiplexer_11_out, multiplexer_12_out, multiplexer_13_out, multiplexer_14_out, multiplexer_15_out,
       multiplexer_16_out, multiplexer_17_out, multiplexer_18_out, multiplexer_19_out, multiplexer_20_out,
       multiplexer_21_out, multiplexer_22_out, multiplexer_23_out, multiplexer_24_out, multiplexer_25_out,
       multiplexer_26_out, multiplexer_27_out, multiplexer_28_out, multiplexer_29_out, multiplexer_30_out,
       multiplexer_31_out, multiplexer_32_out;

  Multiplexer #(.enable("false")) multiplexer_1 (
    .in0(\input [0]), .in1(\input [1]), .out(multiplexer_1_out), .sel(shift[0]));
  Multiplexer #(.enable("false")) multiplexer_2 (
    .in0(\input [1]), .in1(\input [2]), .out(multiplexer_2_out), .sel(shift[0]));
  Multiplexer #(.enable("false")) multiplexer_3 (
    .in0(\input [2]), .in1(\input [3]), .out(multiplexer_3_out), .sel(shift[0]));
  Multiplexer #(.enable("false")) multiplexer_4 (
    .in0(\input [3]), .in1(\input [4]), .out(multiplexer_4_out), .sel(shift[0]));
  Multiplexer #(.enable("false")) multiplexer_5 (
    .in0(\input [4]), .in1(\input [5]), .out(multiplexer_5_out), .sel(shift[0]));
  Multiplexer #(.enable("false")) multiplexer_6 (
    .in0(\input [5]), .in1(\input [6]), .out(multiplexer_6_out), .sel(shift[0]));
  Multiplexer #(.enable("false")) multiplexer_7 (
    .in0(\input [6]), .in1(\input [7]), .out(multiplexer_7_out), .sel(shift[0]));
  Multiplexer #(.enable("false")) multiplexer_8 (
    .in0(\input [7]), .in1(\input [8]), .out(multiplexer_8_out), .sel(shift[0]));
  Multiplexer #(.enable("false")) multiplexer_9 (
    .in0(\input [8]), .in1(\input [9]), .out(multiplexer_9_out), .sel(shift[0]));
  Multiplexer #(.enable("false")) multiplexer_10 (
    .in0(\input [9]), .in1(\input [10]), .out(multiplexer_10_out), .sel(shift[0]));
  Multiplexer #(.enable("false")) multiplexer_11 (
    .in0(\input [10]), .in1(\input [11]), .out(multiplexer_11_out), .sel(shift[0]));
  Multiplexer #(.enable("false")) multiplexer_12 (
    .in0(\input [11]), .in1(\input [12]), .out(multiplexer_12_out), .sel(shift[0]));
  Multiplexer #(.enable("false")) multiplexer_13 (
    .in0(\input [12]), .in1(\input [13]), .out(multiplexer_13_out), .sel(shift[0]));
  Multiplexer #(.enable("false")) multiplexer_14 (
    .in0(\input [13]), .in1(\input [14]), .out(multiplexer_14_out), .sel(shift[0]));
  Multiplexer #(.enable("false")) multiplexer_15 (
    .in0(\input [14]), .in1(\input [15]), .out(multiplexer_15_out), .sel(shift[0]));
  Multiplexer #(.enable("false")) multiplexer_16 (
    .in0(\input [15]), .in1(1'b0), .out(multiplexer_16_out), .sel(shift[0]));
  Multiplexer #(.enable("false")) multiplexer_17 (
    .in0(multiplexer_1_out), .in1(multiplexer_3_out), .out(multiplexer_17_out), .sel(shift[1]));
  Multiplexer #(.enable("false")) multiplexer_18 (
    .in0(multiplexer_2_out), .in1(multiplexer_4_out), .out(multiplexer_18_out), .sel(shift[1]));
  Multiplexer #(.enable("false")) multiplexer_19 (
    .in0(multiplexer_3_out), .in1(multiplexer_5_out), .out(multiplexer_19_out), .sel(shift[1]));
  Multiplexer #(.enable("false")) multiplexer_20 (
    .in0(multiplexer_4_out), .in1(multiplexer_6_out), .out(multiplexer_20_out), .sel(shift[1]));
  Multiplexer #(.enable("false")) multiplexer_21 (
    .in0(multiplexer_5_out), .in1(multiplexer_7_out), .out(multiplexer_21_out), .sel(shift[1]));
  Multiplexer #(.enable("false")) multiplexer_22 (
    .in0(multiplexer_6_out), .in1(multiplexer_8_out), .out(multiplexer_22_out), .sel(shift[1]));
  Multiplexer #(.enable("false")) multiplexer_23 (
    .in0(multiplexer_7_out), .in1(multiplexer_9_out), .out(multiplexer_23_out), .sel(shift[1]));
  Multiplexer #(.enable("false")) multiplexer_24 (
    .in0(multiplexer_8_out), .in1(multiplexer_10_out), .out(multiplexer_24_out), .sel(shift[1]));
  Multiplexer #(.enable("false")) multiplexer_25 (
    .in0(multiplexer_9_out), .in1(multiplexer_11_out), .out(multiplexer_25_out), .sel(shift[1]));
  Multiplexer #(.enable("false")) multiplexer_26 (
    .in0(multiplexer_10_out), .in1(multiplexer_12_out), .out(multiplexer_26_out), .sel(shift[1]));
  Multiplexer #(.enable("false")) multiplexer_27 (
    .in0(multiplexer_11_out), .in1(multiplexer_13_out), .out(multiplexer_27_out), .sel(shift[1]));
  Multiplexer #(.enable("false")) multiplexer_28 (
    .in0(multiplexer_12_out), .in1(multiplexer_14_out), .out(multiplexer_28_out), .sel(shift[1]));
  Multiplexer #(.enable("false")) multiplexer_29 (
    .in0(multiplexer_13_out), .in1(multiplexer_15_out), .out(multiplexer_29_out), .sel(shift[1]));
  Multiplexer #(.enable("false")) multiplexer_30 (
    .in0(multiplexer_14_out), .in1(multiplexer_16_out), .out(multiplexer_30_out), .sel(shift[1]));
  Multiplexer #(.enable("false")) multiplexer_31 (
    .in0(multiplexer_15_out), .in1(1'b0), .out(multiplexer_31_out), .sel(shift[1]));
  Multiplexer #(.enable("false")) multiplexer_32 (
    .in0(multiplexer_16_out), .in1(1'b0), .out(multiplexer_32_out), .sel(shift[1]));
  Multiplexer #(.enable("false")) multiplexer_33 (
    .in0(multiplexer_17_out), .in1(multiplexer_21_out), .out(\output [0]), .sel(shift[2]));
  Multiplexer #(.enable("false")) multiplexer_34 (
    .in0(multiplexer_18_out), .in1(multiplexer_22_out), .out(\output [1]), .sel(shift[2]));
  Multiplexer #(.enable("false")) multiplexer_35 (
    .in0(multiplexer_19_out), .in1(multiplexer_23_out), .out(\output [2]), .sel(shift[2]));
  Multiplexer #(.enable("false")) multiplexer_36 (
    .in0(multiplexer_20_out), .in1(multiplexer_24_out), .out(\output [3]), .sel(shift[2]));
  Multiplexer #(.enable("false")) multiplexer_37 (
    .in0(multiplexer_21_out), .in1(multiplexer_25_out), .out(\output [4]), .sel(shift[2]));
  Multiplexer #(.enable("false")) multiplexer_38 (
    .in0(multiplexer_22_out), .in1(multiplexer_26_out), .out(\output [5]), .sel(shift[2]));
  Multiplexer #(.enable("false")) multiplexer_39 (
    .in0(multiplexer_23_out), .in1(multiplexer_27_out), .out(\output [6]), .sel(shift[2]));
  Multiplexer #(.enable("false")) multiplexer_40 (
    .in0(multiplexer_24_out), .in1(multiplexer_28_out), .out(\output [7]), .sel(shift[2]));
  Multiplexer #(.enable("false")) multiplexer_41 (
    .in0(multiplexer_25_out), .in1(multiplexer_29_out), .out(\output [8]), .sel(shift[2]));
  Multiplexer #(.enable("false")) multiplexer_42 (
    .in0(multiplexer_26_out), .in1(multiplexer_30_out), .out(\output [9]), .sel(shift[2]));
  Multiplexer #(.enable("false")) multiplexer_43 (
    .in0(multiplexer_27_out), .in1(multiplexer_31_out), .out(\output [10]), .sel(shift[2]));
  Multiplexer #(.enable("false")) multiplexer_44 (
    .in0(multiplexer_28_out), .in1(multiplexer_32_out), .out(\output [11]), .sel(shift[2]));
  Multiplexer #(.enable("false")) multiplexer_45 (
    .in0(multiplexer_29_out), .in1(1'b0), .out(\output [12]), .sel(shift[2]));
  Multiplexer #(.enable("false")) multiplexer_46 (
    .in0(multiplexer_30_out), .in1(1'b0), .out(\output [13]), .sel(shift[2]));
  Multiplexer #(.enable("false")) multiplexer_47 (
    .in0(multiplexer_31_out), .in1(1'b0), .out(\output [14]), .sel(shift[2]));
  Multiplexer #(.enable("false")) multiplexer_48 (
    .in0(multiplexer_32_out), .in1(1'b0), .out(\output [15]), .sel(shift[2]));

  // Other names for the same wires on the sheet: b2 = shift[0]; b1 = shift[1]; b0 = shift[2]
endmodule

module control (
  input  [4:0] Opcode,
  input  [4:0] ALUop,
  output SwC,
  output Rwe,
  output PConeNC,
  output PCTC,
  output ALUinB,
  output PCRdC,
  output RstatusC,
  output BNEC,
  output BLTC,
  output JalC,
  output BEXC,
  output DMwe,
  output DMld,
  output RsC,
  output MEMwrite,
  output ALUopAddC,
  output Rdc,
  output SETXC
);

  wire add, addi, \and , div, j, mul, \or , sll, sra, sub;

  control_decoder control_decoder_1 (
    .Opcode(Opcode), .j(j), .bne(BNEC), .jal(JalC), .jr(PCRdC), .blt(BLTC), .addi(addi), .sw(DMwe),
    .lw(DMld), .setx(RstatusC), .bex(BEXC), .ALUop(ALUop), .add(add), .sub(sub), .\and (\and ), .\or (\or ),
    .sll(sll), .sra(sra), .mul(mul), .div(div));
  or or_1 (Rwe, add, addi, sub, \and , \or , sll, sra, mul, div, DMld, JalC, RstatusC);
  or or_2 (ALUinB, addi, DMwe, DMld, RstatusC);
  buf or_3 (MEMwrite, DMld);  // OR_Gate
  or or_4 (Rdc, PCRdC, BNEC, BLTC);
  or or_5 (PCTC, j, JalC);
  or or_6 (RsC, BNEC, BLTC);
  or or_7 (ALUopAddC, DMld, DMwe, RstatusC, addi);

  assign PConeNC = 1'b0;
  assign SETXC = RstatusC;
  assign SwC = DMwe;

  // Other names for the same wires on the sheet: bex = BEXC; blt = BLTC; bne = BNEC; jal = JalC; jr = PCRdC;
  //   lw = DMld; setx = RstatusC; sw = DMwe
endmodule

module control_decoder (
  input  [4:0] Opcode,
  input  [4:0] ALUop,
  output j,
  output bne,
  output jal,
  output jr,
  output blt,
  output addi,
  output sw,
  output lw,
  output setx,
  output bex,
  output add,
  output sub,
  output \and ,
  output \or ,
  output sll,
  output sra,
  output mul,
  output div
);

  wire alu_operation, decoder_2_out0, decoder_2_out1, decoder_2_out2, decoder_2_out3, decoder_2_out4,
       decoder_2_out5, decoder_2_out6, decoder_2_out7;

  Decoder #(.select(5), .enable("false")) decoder_1 (
    .out0(alu_operation), .out1(j), .out2(bne), .out3(jal), .out4(jr), .out5(addi), .out6(blt), .out7(sw),
    .out8(lw), .out21(setx), .out22(bex), .sel(Opcode));  // open: out9, out10, out11, out12, out13, out14, out15, out16, out17, out18, out19, out20, out23, out24, out25, out26, out27, out28, out29, out30, out31
  Decoder #(.select(5), .enable("false")) decoder_2 (
    .out0(decoder_2_out0), .out1(decoder_2_out1), .out2(decoder_2_out2), .out3(decoder_2_out3),
    .out4(decoder_2_out4), .out5(decoder_2_out5), .out6(decoder_2_out6), .out7(decoder_2_out7), .sel(ALUop));  // open: out8, out9, out10, out11, out12, out13, out14, out15, out16, out17, out18, out19, out20, out21, out22, out23, out24, out25, out26, out27, out28, out29, out30, out31
  and and_1 (add, decoder_2_out0, alu_operation);
  and and_2 (sub, decoder_2_out1, alu_operation);
  and and_3 (\and , decoder_2_out2, alu_operation);
  and and_4 (\or , decoder_2_out3, alu_operation);
  and and_5 (sll, decoder_2_out4, alu_operation);
  and and_6 (sra, decoder_2_out5, alu_operation);
  and and_7 (mul, decoder_2_out6, alu_operation);
  and and_8 (div, decoder_2_out7, alu_operation);
endmodule

module multiplier (
  input  other_ctrl,
  input  [8:0] multiplier,
  input  ctrlMULT,
  input  clk,
  input  [7:0] multiplicand,
  output data_mult_rdy,
  output [15:0] data_result_mult
);

  wire a, adder_1_cout, and_1_out, and_2_out, and_3_out, and_4_out, and_5_out, and_6_out, and_7_out,
       and_9_out, b, c, c0, not_1_out, not_2_out, not_3_out, not_4_out, not_6_out, not_7_out, not_8_out,
       not_9_out, not_10_out, not_11_out, not_12_out, not_13_out, not_14_out, not_15_out, not_16_out,
       not_17_out, not_18_out, not_19_out, not_20_out, not_21_out, or_1_out, overflow_a, overflow_s,
       register_32_2_p3, register_32_2_p5;
  wire [0:0] register_32_2_p4;
  wire [7:0] adder_2_out, adder_3_out, multiplexer_1_out, multiplexer_2_out, multiplexer_3_out,
       multiplexer_5_out, not_5_out, shifter_1_out;
  wire [14:0] register_32_2_p4_2;
  wire [15:0] adder_4_out, adder_5_out, register_32_1_p2, register_32_1_p4, register_32_3_p4;
  wire [16:0] multiplexer_4_out, multiplexer_7_out, shifter_2_out;

  // Probe on register_32_1_p4
  // register_32 register_32_1: pin names not known; wires that end beside it: clk, register_32_1_p2, 1'b1, register_32_1_p4, ctrlMULT
  Adder #(.width(16)) adder_1 (
    .a(register_32_1_p4), .b({16{1'b0}}), .out(register_32_1_p2), .cin(or_1_out), .cout(adder_1_cout));
  not not_1 (not_1_out, c0);
  not not_2 (not_2_out, data_result_mult[0]);
  and and_1 (and_1_out, not_1_out, not_2_out, data_result_mult[1]);
  not not_3 (not_3_out, data_result_mult[0]);
  and and_2 (and_2_out, c0, not_3_out, data_result_mult[1]);
  not not_4 (not_4_out, c0);
  and and_3 (and_3_out, not_4_out, data_result_mult[0], data_result_mult[1]);
  or or_1 (or_1_out, overflow_a, 1'b0);
  Shifter shifter_1 (.in(multiplicand), .\dist (3'b001), .out(shifter_1_out));
  or or_2 (a, and_1_out, and_2_out, and_3_out);
  Multiplexer #(.width(8), .enable("false")) multiplexer_1 (
    .in0(multiplicand), .in1(shifter_1_out), .out(multiplexer_1_out), .sel(b));
  Multiplexer #(.width(8), .enable("false")) multiplexer_2 (
    .in0(multiplexer_1_out), .in1(not_5_out), .out(multiplexer_2_out), .sel(a));
  assign not_5_out = ~multiplexer_1_out;  // NOT_Gate not_5, 8 bits wide
  and and_4 (and_4_out, c0, data_result_mult[0], not_6_out);
  not not_6 (not_6_out, data_result_mult[1]);
  not not_7 (not_7_out, c0);
  and and_5 (and_5_out, not_7_out, not_8_out, data_result_mult[1]);
  not not_8 (not_8_out, data_result_mult[0]);
  and and_6 (and_6_out, c0, data_result_mult[0], data_result_mult[1]);
  not not_9 (not_9_out, c0);
  not not_10 (not_10_out, data_result_mult[0]);
  and and_7 (and_7_out, not_9_out, not_10_out, not_11_out);
  not not_11 (not_11_out, data_result_mult[1]);
  Multiplexer #(.width(8), .enable("false")) multiplexer_3 (
    .in0(multiplexer_2_out), .in1({8{1'b0}}), .out(multiplexer_3_out), .sel(c));
  // Probe on multiplexer_3_out
  or or_3 (b, and_4_out, and_5_out);
  or or_4 (c, and_6_out, and_7_out);
  // Probe on data_result_mult[15:8]
  // Probe on {data_result_mult, c0}
  Adder adder_2 (.a(multiplexer_3_out), .b(data_result_mult[15:8]), .out(adder_2_out), .cin(1'b0), .cout(overflow_a));
  Adder adder_3 (.a(multiplexer_3_out), .b(data_result_mult[15:8]), .out(adder_3_out), .cin(1'b1), .cout(overflow_s));
  Multiplexer #(.width(9), .enable("false")) multiplexer_4 (
    .in0({data_result_mult[7:0], c0}), .in1(multiplier), .out(multiplexer_4_out[8:0]), .sel(ctrlMULT));
  Multiplexer #(.width(8), .enable("false")) multiplexer_5 (
    .in0(adder_2_out), .in1(adder_3_out), .out(multiplexer_5_out), .sel(a));
  Multiplexer #(.width(8), .enable("false")) multiplexer_6 (
    .in0(multiplexer_5_out), .in1({8{1'b0}}), .out(multiplexer_4_out[16:9]), .sel(ctrlMULT));
  Adder #(.width(16)) adder_4 (
    .a({register_32_2_p4_2, register_32_2_p4[0]}), .b(16'h1), .out(adder_4_out), .cin(1'b0));  // open: cout
  // Probe on multiplexer_4_out[8:0]
  // Probe on multiplexer_4_out[16:9]
  Adder #(.width(16)) adder_5 (.a(register_32_3_p4), .b(16'h1), .out(adder_5_out), .cin(1'b0));  // open: cout
  // Probe on {register_32_2_p4_2, register_32_2_p4[0]}
  // register_32 register_32_2: pin names not known; wires that end beside it: clk, adder_4_out, register_32_2_p3, {register_32_2_p4_2, register_32_2_p4[0]}, register_32_2_p5
  and and_8 (register_32_2_p3, ctrlMULT, not_14_out);
  and and_9 (and_9_out, not_12_out, not_13_out);
  // Probe on register_32_3_p4
  // register_32 register_32_3: pin names not known; wires that end beside it: clk, adder_5_out, 1'b1, register_32_3_p4, ctrlMULT
  buf or_5 (register_32_2_p5, other_ctrl);  // OR_Gate
  register_17 register_17_1 (
    .clk(clk), .\input (multiplexer_7_out), .enable(clk), .\output ({data_result_mult, c0}), .reset(1'b0));
  Multiplexer #(.width(17), .enable("false")) multiplexer_7 (
    .in0(multiplexer_4_out), .in1(shifter_2_out), .out(multiplexer_7_out), .sel(and_9_out));
  Shifter #(.width(17), .shift("ar")) shifter_2 (.in(multiplexer_4_out), .\dist (5'b00010), .out(shifter_2_out));
  not not_12 (not_12_out, clk);
  not not_13 (not_13_out, ctrlMULT);
  not not_14 (not_14_out, register_32_2_p4[0]);
  // Probe on {data_result_mult, c0}
  not not_15 (not_15_out, register_32_3_p4[0]);
  not not_16 (not_16_out, register_32_3_p4[1]);
  not not_17 (not_17_out, register_32_3_p4[3]);
  not not_18 (not_18_out, register_32_3_p4[4]);
  not not_19 (not_19_out, register_32_3_p4[5]);
  not not_20 (not_20_out, register_32_3_p4[6]);
  not not_21 (not_21_out, register_32_3_p4[7]);
  // Probe on multiplexer_7_out
  and and_10 (data_mult_rdy, not_15_out, not_16_out, register_32_3_p4[2], not_17_out, not_18_out, not_19_out, not_20_out, not_21_out);

  // Other names for the same wires on the sheet: c1 = data_result_mult[0]; c2 = data_result_mult[1];
  //   data_rdy = data_mult_rdy
endmodule

module register_17 (
  input  clk,
  input  [16:0] \input ,
  input  enable,
  input  reset,
  output [16:0] \output 
);

  D_Flip_Flop d_ff_1 (.clk(clk), .D(\input [0]), .Q(\output [0]), .en(enable), .reset(reset));  // open: Qn, preset
  D_Flip_Flop d_ff_2 (.clk(clk), .D(\input [4]), .Q(\output [4]), .en(enable), .reset(reset));  // open: Qn, preset
  D_Flip_Flop d_ff_3 (.clk(clk), .D(\input [8]), .Q(\output [8]), .en(enable), .reset(reset));  // open: Qn, preset
  D_Flip_Flop d_ff_4 (.clk(clk), .D(\input [12]), .Q(\output [12]), .en(enable), .reset(reset));  // open: Qn, preset
  D_Flip_Flop d_ff_5 (.clk(clk), .D(\input [16]), .Q(\output [16]), .en(enable), .reset(reset));  // open: Qn, preset
  D_Flip_Flop d_ff_6 (.clk(clk), .D(\input [1]), .Q(\output [1]), .en(enable), .reset(reset));  // open: Qn, preset
  D_Flip_Flop d_ff_7 (.clk(clk), .D(\input [5]), .Q(\output [5]), .en(enable), .reset(reset));  // open: Qn, preset
  D_Flip_Flop d_ff_8 (.clk(clk), .D(\input [9]), .Q(\output [9]), .en(enable), .reset(reset));  // open: Qn, preset
  D_Flip_Flop d_ff_9 (.clk(clk), .D(\input [13]), .Q(\output [13]), .en(enable), .reset(reset));  // open: Qn, preset
  D_Flip_Flop d_ff_10 (.clk(clk), .D(\input [2]), .Q(\output [2]), .en(enable), .reset(reset));  // open: Qn, preset
  D_Flip_Flop d_ff_11 (.clk(clk), .D(\input [6]), .Q(\output [6]), .en(enable), .reset(reset));  // open: Qn, preset
  D_Flip_Flop d_ff_12 (.clk(clk), .D(\input [10]), .Q(\output [10]), .en(enable), .reset(reset));  // open: Qn, preset
  D_Flip_Flop d_ff_13 (.clk(clk), .D(\input [14]), .Q(\output [14]), .en(enable), .reset(reset));  // open: Qn, preset
  D_Flip_Flop d_ff_14 (.clk(clk), .D(\input [3]), .Q(\output [3]), .en(enable), .reset(reset));  // open: Qn, preset
  D_Flip_Flop d_ff_15 (.clk(clk), .D(\input [7]), .Q(\output [7]), .en(enable), .reset(reset));  // open: Qn, preset
  D_Flip_Flop d_ff_16 (.clk(clk), .D(\input [11]), .Q(\output [11]), .en(enable), .reset(reset));  // open: Qn, preset
  D_Flip_Flop d_ff_17 (.clk(clk), .D(\input [15]), .Q(\output [15]), .en(enable), .reset(reset));  // open: Qn, preset
endmodule

module divider (
  input  other_ctrl,
  input  ctrlDIV,
  input  clk,
  input  [7:0] divisor,
  input  [7:0] dividend,
  output [15:0] data_result_div,
  output data_rdy_div
);

  wire and_1_out, not_1_out, not_2_out, not_3_out, not_4_out, not_5_out, not_6_out, not_7_out, not_8_out,
       not_10_out, register_32_2_p5;
  wire [0:0] multiplexer_3_out_2;
  wire [7:0] adder_3_out, not_9_out;
  wire [15:0] adder_1_out, adder_2_out, adder_4_out, multiplexer_1_out, multiplexer_2_out, register_32_1_p5,
       register_32_2_p4, shifter_1_out, shifter_2_out, shifter_3_out;
  wire [15:1] multiplexer_3_out;

  Adder #(.width(16)) adder_1 (.a(register_32_2_p4), .b(16'h1), .out(adder_1_out), .cin(1'b0));  // open: cout
  Adder #(.width(16)) adder_2 (.a(register_32_1_p5), .b(16'h1), .out(adder_2_out), .cin(1'b0));  // open: cout
  and and_1 (and_1_out, ctrlDIV, not_1_out);
  Multiplexer #(.width(16), .enable("false")) multiplexer_1 (
    .in0(multiplexer_2_out), .in1(shifter_1_out), .out(multiplexer_1_out), .sel(ctrlDIV));
  Shifter #(.width(16)) shifter_1 (.in({{8{1'b0}}, dividend}), .\dist (4'b0001), .out(shifter_1_out));
  // Probe on register_32_1_p5
  // register_32 register_32_1: pin names not known; wires that end beside it: clk, adder_2_out, 1'b1, 1'b0, register_32_1_p5, ctrlDIV
  // Probe on register_32_2_p4
  // register_32 register_32_2: pin names not known; wires that end beside it: clk, adder_1_out, and_1_out, register_32_2_p4, register_32_2_p5
  buf or_1 (register_32_2_p5, other_ctrl);  // OR_Gate
  not not_1 (not_1_out, register_32_2_p4[0]);
  // Probe on multiplexer_1_out
  not not_2 (not_2_out, register_32_1_p5[0]);
  not not_3 (not_3_out, register_32_1_p5[1]);
  not not_4 (not_4_out, register_32_1_p5[2]);
  not not_5 (not_5_out, register_32_1_p5[4]);
  not not_6 (not_6_out, register_32_1_p5[5]);
  not not_7 (not_7_out, register_32_1_p5[6]);
  not not_8 (not_8_out, register_32_1_p5[7]);
  // register_32 register_32_3: pin names not known; wires that end beside it: clk, multiplexer_1_out, 1'b1, data_result_div, 1'b0, ctrlDIV
  // Probe on data_result_div
  and and_2 (data_rdy_div, not_2_out, not_3_out, not_4_out, register_32_1_p5[3], not_5_out, not_6_out, not_7_out, not_8_out);
  assign not_9_out = ~divisor;  // NOT_Gate not_9, 8 bits wide
  Shifter #(.width(16)) shifter_2 (.in(data_result_div), .\dist (4'b0001), .out(shifter_2_out));
  Adder adder_3 (.a(not_9_out), .b({8{1'b0}}), .out(adder_3_out), .cin(1'b1));  // open: cout
  // Probe on multiplexer_2_out
  Multiplexer #(.width(16), .enable("false")) multiplexer_2 (
    .in0({multiplexer_3_out, 1'b1}), .in1(shifter_2_out), .out(multiplexer_2_out), .sel(adder_4_out[15]));
  Adder #(.width(16)) adder_4 (
    .a(data_result_div), .b({adder_3_out, {8{1'b0}}}), .out(adder_4_out), .cin(1'b0));  // open: cout
  // Probe on adder_4_out
  Shifter #(.width(16)) shifter_3 (.in(adder_4_out), .\dist (4'b0001), .out(shifter_3_out));
  // Probe on {adder_3_out, {8{1'b0}}}
  Multiplexer #(.width(16), .enable("false")) multiplexer_3 (
    .in0(adder_4_out), .in1(shifter_3_out), .out({multiplexer_3_out, multiplexer_3_out_2[0]}),
    .sel(not_10_out));
  not not_10 (not_10_out, clk);
endmodule

module register_8 (
  input  clk,
  input  [7:0] \input ,
  input  enable,
  input  reset,
  output [7:0] \output 
);

  wire d_ff_3_q, d_ff_4_q, d_ff_7_q, d_ff_8_q, d_ff_11_q, d_ff_12_q, d_ff_15_q, d_ff_16_q, undriven,
       undriven_2, undriven_3, undriven_4, undriven_5, undriven_6, undriven_7, undriven_8;

  D_Flip_Flop d_ff_1 (.clk(clk), .D(\input [0]), .Q(\output [0]), .en(enable), .reset(reset));  // open: Qn, preset
  D_Flip_Flop d_ff_2 (.clk(clk), .D(\input [4]), .Q(\output [4]), .en(enable), .reset(reset));  // open: Qn, preset
  D_Flip_Flop d_ff_3 (.clk(clk), .D(undriven), .Q(d_ff_3_q), .en(enable), .reset(reset));  // open: Qn, preset
  D_Flip_Flop d_ff_4 (.clk(clk), .D(undriven_5), .Q(d_ff_4_q), .en(enable), .reset(reset));  // open: Qn, preset
  D_Flip_Flop d_ff_5 (.clk(clk), .D(\input [1]), .Q(\output [1]), .en(enable), .reset(reset));  // open: Qn, preset
  D_Flip_Flop d_ff_6 (.clk(clk), .D(\input [5]), .Q(\output [5]), .en(enable), .reset(reset));  // open: Qn, preset
  D_Flip_Flop d_ff_7 (.clk(clk), .D(undriven_2), .Q(d_ff_7_q), .en(enable), .reset(reset));  // open: Qn, preset
  D_Flip_Flop d_ff_8 (.clk(clk), .D(undriven_6), .Q(d_ff_8_q), .en(enable), .reset(reset));  // open: Qn, preset
  D_Flip_Flop d_ff_9 (.clk(clk), .D(\input [2]), .Q(\output [2]), .en(enable), .reset(reset));  // open: Qn, preset
  D_Flip_Flop d_ff_10 (.clk(clk), .D(\input [6]), .Q(\output [6]), .en(enable), .reset(reset));  // open: Qn, preset
  D_Flip_Flop d_ff_11 (.clk(clk), .D(undriven_3), .Q(d_ff_11_q), .en(enable), .reset(reset));  // open: Qn, preset
  D_Flip_Flop d_ff_12 (.clk(clk), .D(undriven_7), .Q(d_ff_12_q), .en(enable), .reset(reset));  // open: Qn, preset
  D_Flip_Flop d_ff_13 (.clk(clk), .D(\input [3]), .Q(\output [3]), .en(enable), .reset(reset));  // open: Qn, preset
  D_Flip_Flop d_ff_14 (.clk(clk), .D(\input [7]), .Q(\output [7]), .en(enable), .reset(reset));  // open: Qn, preset
  D_Flip_Flop d_ff_15 (.clk(clk), .D(undriven_4), .Q(d_ff_15_q), .en(enable), .reset(reset));  // open: Qn, preset
  D_Flip_Flop d_ff_16 (.clk(clk), .D(undriven_8), .Q(d_ff_16_q), .en(enable), .reset(reset));  // open: Qn, preset
endmodule

module multdiv (
  input  [7:0] data_operandA,
  input  [7:0] data_operandB,
  input  ctrl_DIV,
  input  ctrl_MULT,
  output data_rdy_mult,
  output data_resultRDY,
  output [15:0] data_result,
  output data_rdy_div
);

  wire clk, divider_1_data_rdy_div, multiplier_1_data_mult_rdy;
  wire [15:0] divider_1_data_result_div, multiplier_1_data_result_mult, register_32_1_p4, register_32_2_p4;

  Clock clock_1 (.out(clk));
  multiplier multiplier_1 (
    .other_ctrl(ctrl_DIV), .multiplier({data_operandB, 1'b0}), .ctrlMULT(ctrl_MULT), .clk(clk),
    .multiplicand(data_operandA), .data_mult_rdy(multiplier_1_data_mult_rdy),
    .data_result_mult(multiplier_1_data_result_mult));
  assign data_result = data_rdy_mult ? multiplier_1_data_result_mult : 16'bz;  // Controlled_Buffer controlled_buffer_1
  divider divider_1 (
    .other_ctrl(ctrl_MULT), .ctrlDIV(ctrl_DIV), .clk(clk), .divisor(data_operandB), .dividend(data_operandA),
    .data_result_div(divider_1_data_result_div), .data_rdy_div(divider_1_data_rdy_div));
  assign data_result = data_rdy_div ? divider_1_data_result_div : 16'bz;  // Controlled_Buffer controlled_buffer_2
  // register_32 register_32_1: pin names not known; wires that end beside it: clk, {{15{1'b0}}, ctrl_MULT}, ctrl_MULT, register_32_1_p4, ctrl_DIV
  and and_1 (data_rdy_div, divider_1_data_rdy_div, register_32_2_p4[0]);
  // register_32 register_32_2: pin names not known; wires that end beside it: clk, {{15{1'b0}}, ctrl_DIV}, ctrl_DIV, register_32_2_p4, ctrl_MULT
  and and_2 (data_rdy_mult, register_32_1_p4[0], multiplier_1_data_mult_rdy);
  assign data_resultRDY = data_rdy_mult ? data_rdy_mult : 1'bz;  // Controlled_Buffer controlled_buffer_3
  assign data_resultRDY = data_rdy_div ? data_rdy_div : 1'bz;  // Controlled_Buffer controlled_buffer_4
endmodule

module register_16 (
  input  clk,
  input  [15:0] \input ,
  input  enable,
  input  reset,
  output [15:0] \output 
);

  D_Flip_Flop d_ff_1 (.clk(clk), .D(\input [0]), .Q(\output [0]), .en(enable), .reset(reset));  // open: Qn, preset
  D_Flip_Flop d_ff_2 (.clk(clk), .D(\input [4]), .Q(\output [4]), .en(enable), .reset(reset));  // open: Qn, preset
  D_Flip_Flop d_ff_3 (.clk(clk), .D(\input [8]), .Q(\output [8]), .en(enable), .reset(reset));  // open: Qn, preset
  D_Flip_Flop d_ff_4 (.clk(clk), .D(\input [12]), .Q(\output [12]), .en(enable), .reset(reset));  // open: Qn, preset
  D_Flip_Flop d_ff_5 (.clk(clk), .D(\input [1]), .Q(\output [1]), .en(enable), .reset(reset));  // open: Qn, preset
  D_Flip_Flop d_ff_6 (.clk(clk), .D(\input [5]), .Q(\output [5]), .en(enable), .reset(reset));  // open: Qn, preset
  D_Flip_Flop d_ff_7 (.clk(clk), .D(\input [9]), .Q(\output [9]), .en(enable), .reset(reset));  // open: Qn, preset
  D_Flip_Flop d_ff_8 (.clk(clk), .D(\input [13]), .Q(\output [13]), .en(enable), .reset(reset));  // open: Qn, preset
  D_Flip_Flop d_ff_9 (.clk(clk), .D(\input [2]), .Q(\output [2]), .en(enable), .reset(reset));  // open: Qn, preset
  D_Flip_Flop d_ff_10 (.clk(clk), .D(\input [6]), .Q(\output [6]), .en(enable), .reset(reset));  // open: Qn, preset
  D_Flip_Flop d_ff_11 (.clk(clk), .D(\input [10]), .Q(\output [10]), .en(enable), .reset(reset));  // open: Qn, preset
  D_Flip_Flop d_ff_12 (.clk(clk), .D(\input [14]), .Q(\output [14]), .en(enable), .reset(reset));  // open: Qn, preset
  D_Flip_Flop d_ff_13 (.clk(clk), .D(\input [3]), .Q(\output [3]), .en(enable), .reset(reset));  // open: Qn, preset
  D_Flip_Flop d_ff_14 (.clk(clk), .D(\input [7]), .Q(\output [7]), .en(enable), .reset(reset));  // open: Qn, preset
  D_Flip_Flop d_ff_15 (.clk(clk), .D(\input [11]), .Q(\output [11]), .en(enable), .reset(reset));  // open: Qn, preset
  D_Flip_Flop d_ff_16 (.clk(clk), .D(\input [15]), .Q(\output [15]), .en(enable), .reset(reset));  // open: Qn, preset
endmodule

module _32_bit_add (
  input  a31,
  input  b31,
  input  a30,
  input  b30,
  input  a29,
  input  b29,
  input  a28,
  input  b28,
  input  a27,
  input  b27,
  input  a26,
  input  b26,
  input  a25,
  input  b25,
  input  a24,
  input  b24,
  input  a23,
  input  b23,
  input  a22,
  input  b22,
  input  a21,
  input  b21,
  input  a20,
  input  b20,
  input  a19,
  input  b19,
  input  a18,
  input  b18,
  input  a17,
  input  b17,
  input  a16,
  input  b16,
  input  add_sub,
  input  a15,
  input  b15,
  input  a14,
  input  b14,
  input  a13,
  input  b13,
  input  a12,
  input  b12,
  input  a11,
  input  b11,
  input  a10,
  input  b10,
  input  a9,
  input  b9,
  input  a8,
  input  b8,
  input  a7,
  input  b7,
  input  a6,
  input  b6,
  input  a5,
  input  b5,
  input  a4,
  input  b4,
  input  a3,
  input  b3,
  input  a2,
  input  b2,
  input  a1,
  input  b1,
  input  a0,
  input  b0,
  output ovf,
  output s31,
  output s30,
  output s29,
  output s28,
  output s27,
  output s26,
  output s25,
  output s24,
  output cout,
  output s23,
  output s22,
  output s21,
  output s20,
  output s19,
  output s18,
  output s17,
  output s16,
  output s15,
  output s14,
  output s13,
  output s12,
  output s11,
  output s10,
  output s9,
  output s8,
  output s7,
  output s6,
  output s5,
  output s4,
  output s3,
  output s2,
  output s1,
  output s0
);

  wire one_bit_add_2_cout, one_bit_add_3_cout, one_bit_add_4_cout, one_bit_add_5_cout, one_bit_add_6_cout,
       one_bit_add_7_cout, one_bit_add_8_cout, one_bit_add_9_cout, one_bit_add_10_cout, one_bit_add_11_cout,
       one_bit_add_12_cout, one_bit_add_13_cout, one_bit_add_14_cout, one_bit_add_15_cout,
       one_bit_add_16_cout, one_bit_add_17_cout, one_bit_add_18_cout, one_bit_add_19_cout,
       one_bit_add_20_cout, one_bit_add_21_cout, one_bit_add_22_cout, one_bit_add_23_cout,
       one_bit_add_24_cout, one_bit_add_25_cout, one_bit_add_26_cout, one_bit_add_27_cout,
       one_bit_add_28_cout, one_bit_add_29_cout, one_bit_add_30_cout, one_bit_add_31_cout,
       one_bit_add_32_cout, xor_2_out, xor_3_out, xor_4_out, xor_5_out, xor_6_out, xor_7_out, xor_8_out,
       xor_9_out, xor_10_out, xor_11_out, xor_12_out, xor_13_out, xor_14_out, xor_15_out, xor_16_out,
       xor_17_out, xor_18_out, xor_19_out, xor_20_out, xor_21_out, xor_22_out, xor_23_out, xor_24_out,
       xor_25_out, xor_26_out, xor_27_out, xor_28_out, xor_29_out, xor_30_out, xor_31_out, xor_32_out,
       xor_33_out;

  xor xor_1 (ovf, cout, one_bit_add_5_cout);
  one_bit_add one_bit_add_1 (.a(a31), .b(xor_2_out), .cout(cout), .cin(one_bit_add_5_cout), .sum(s31));
  xor xor_2 (xor_2_out, add_sub, b31);
  one_bit_add one_bit_add_2 (.a(a23), .b(xor_3_out), .cout(one_bit_add_2_cout), .cin(one_bit_add_6_cout), .sum(s23));
  xor xor_3 (xor_3_out, add_sub, b23);
  one_bit_add one_bit_add_3 (.a(a15), .b(xor_4_out), .cout(one_bit_add_3_cout), .cin(one_bit_add_7_cout), .sum(s15));
  xor xor_4 (xor_4_out, add_sub, b15);
  one_bit_add one_bit_add_4 (.a(a7), .b(xor_5_out), .cout(one_bit_add_4_cout), .cin(one_bit_add_8_cout), .sum(s7));
  xor xor_5 (xor_5_out, add_sub, b7);
  one_bit_add one_bit_add_5 (.a(a30), .b(xor_6_out), .cout(one_bit_add_5_cout), .cin(one_bit_add_9_cout), .sum(s30));
  xor xor_6 (xor_6_out, add_sub, b30);
  one_bit_add one_bit_add_6 (.a(a22), .b(xor_7_out), .cout(one_bit_add_6_cout), .cin(one_bit_add_10_cout), .sum(s22));
  xor xor_7 (xor_7_out, add_sub, b22);
  one_bit_add one_bit_add_7 (.a(a14), .b(xor_8_out), .cout(one_bit_add_7_cout), .cin(one_bit_add_11_cout), .sum(s14));
  xor xor_8 (xor_8_out, add_sub, b14);
  one_bit_add one_bit_add_8 (.a(a6), .b(xor_9_out), .cout(one_bit_add_8_cout), .cin(one_bit_add_12_cout), .sum(s6));
  xor xor_9 (xor_9_out, add_sub, b6);
  one_bit_add one_bit_add_9 (.a(a29), .b(xor_10_out), .cout(one_bit_add_9_cout), .cin(one_bit_add_13_cout), .sum(s29));
  xor xor_10 (xor_10_out, add_sub, b29);
  one_bit_add one_bit_add_10 (
    .a(a21), .b(xor_11_out), .cout(one_bit_add_10_cout), .cin(one_bit_add_14_cout), .sum(s21));
  xor xor_11 (xor_11_out, add_sub, b21);
  one_bit_add one_bit_add_11 (
    .a(a13), .b(xor_12_out), .cout(one_bit_add_11_cout), .cin(one_bit_add_15_cout), .sum(s13));
  xor xor_12 (xor_12_out, add_sub, b13);
  one_bit_add one_bit_add_12 (.a(a5), .b(xor_13_out), .cout(one_bit_add_12_cout), .cin(one_bit_add_16_cout), .sum(s5));
  xor xor_13 (xor_13_out, add_sub, b5);
  one_bit_add one_bit_add_13 (
    .a(a28), .b(xor_14_out), .cout(one_bit_add_13_cout), .cin(one_bit_add_17_cout), .sum(s28));
  xor xor_14 (xor_14_out, add_sub, b28);
  one_bit_add one_bit_add_14 (
    .a(a20), .b(xor_15_out), .cout(one_bit_add_14_cout), .cin(one_bit_add_18_cout), .sum(s20));
  xor xor_15 (xor_15_out, add_sub, b20);
  one_bit_add one_bit_add_15 (
    .a(a12), .b(xor_16_out), .cout(one_bit_add_15_cout), .cin(one_bit_add_19_cout), .sum(s12));
  xor xor_16 (xor_16_out, add_sub, b12);
  one_bit_add one_bit_add_16 (.a(a4), .b(xor_17_out), .cout(one_bit_add_16_cout), .cin(one_bit_add_20_cout), .sum(s4));
  one_bit_add one_bit_add_17 (
    .a(a27), .b(xor_18_out), .cout(one_bit_add_17_cout), .cin(one_bit_add_21_cout), .sum(s27));
  one_bit_add one_bit_add_18 (
    .a(a19), .b(xor_19_out), .cout(one_bit_add_18_cout), .cin(one_bit_add_22_cout), .sum(s19));
  one_bit_add one_bit_add_19 (
    .a(a11), .b(xor_20_out), .cout(one_bit_add_19_cout), .cin(one_bit_add_23_cout), .sum(s11));
  one_bit_add one_bit_add_20 (.a(a3), .b(xor_21_out), .cout(one_bit_add_20_cout), .cin(one_bit_add_25_cout), .sum(s3));
  xor xor_17 (xor_17_out, add_sub, b4);
  one_bit_add one_bit_add_21 (
    .a(a26), .b(xor_22_out), .cout(one_bit_add_21_cout), .cin(one_bit_add_24_cout), .sum(s26));
  xor xor_18 (xor_18_out, add_sub, b27);
  one_bit_add one_bit_add_22 (
    .a(a18), .b(xor_23_out), .cout(one_bit_add_22_cout), .cin(one_bit_add_26_cout), .sum(s18));
  xor xor_19 (xor_19_out, add_sub, b19);
  one_bit_add one_bit_add_23 (
    .a(a10), .b(xor_24_out), .cout(one_bit_add_23_cout), .cin(one_bit_add_27_cout), .sum(s10));
  xor xor_20 (xor_20_out, add_sub, b11);
  xor xor_21 (xor_21_out, add_sub, b3);
  one_bit_add one_bit_add_24 (
    .a(a25), .b(xor_26_out), .cout(one_bit_add_24_cout), .cin(one_bit_add_29_cout), .sum(s25));
  xor xor_22 (xor_22_out, add_sub, b26);
  xor xor_23 (xor_23_out, add_sub, b18);
  xor xor_24 (xor_24_out, add_sub, b10);
  one_bit_add one_bit_add_25 (.a(a2), .b(xor_25_out), .cout(one_bit_add_25_cout), .cin(one_bit_add_28_cout), .sum(s2));
  xor xor_25 (xor_25_out, add_sub, b2);
  xor xor_26 (xor_26_out, add_sub, b25);
  one_bit_add one_bit_add_26 (
    .a(a17), .b(xor_27_out), .cout(one_bit_add_26_cout), .cin(one_bit_add_30_cout), .sum(s17));
  xor xor_27 (xor_27_out, add_sub, b17);
  one_bit_add one_bit_add_27 (.a(a9), .b(xor_28_out), .cout(one_bit_add_27_cout), .cin(one_bit_add_31_cout), .sum(s9));
  xor xor_28 (xor_28_out, add_sub, b9);
  one_bit_add one_bit_add_28 (.a(a1), .b(xor_29_out), .cout(one_bit_add_28_cout), .cin(one_bit_add_32_cout), .sum(s1));
  xor xor_29 (xor_29_out, add_sub, b1);
  one_bit_add one_bit_add_29 (.a(a24), .b(xor_30_out), .cout(one_bit_add_29_cout), .cin(one_bit_add_2_cout), .sum(s24));
  xor xor_30 (xor_30_out, add_sub, b24);
  one_bit_add one_bit_add_30 (.a(a16), .b(xor_31_out), .cout(one_bit_add_30_cout), .cin(one_bit_add_3_cout), .sum(s16));
  xor xor_31 (xor_31_out, add_sub, b16);
  one_bit_add one_bit_add_31 (.a(a8), .b(xor_32_out), .cout(one_bit_add_31_cout), .cin(one_bit_add_4_cout), .sum(s8));
  xor xor_32 (xor_32_out, add_sub, b8);
  one_bit_add one_bit_add_32 (.a(a0), .b(xor_33_out), .cout(one_bit_add_32_cout), .cin(add_sub), .sum(s0));
  xor xor_33 (xor_33_out, add_sub, b0);
endmodule

module _32_bit_compact (
  input  [31:0] A,
  input  [31:0] B,
  input  sub,
  output ovf,
  output [31:0] result
);

  _32_bit_add u_32_bit_add_1 (
    .add_sub(sub), .ovf(ovf), .s7(result[7]), .s31(result[31]), .s23(result[23]), .s15(result[15]),
    .s30(result[30]), .s22(result[22]), .s14(result[14]), .s6(result[6]), .s29(result[29]), .s21(result[21]),
    .s13(result[13]), .s5(result[5]), .s28(result[28]), .s20(result[20]), .s12(result[12]), .s4(result[4]),
    .s27(result[27]), .s19(result[19]), .s11(result[11]), .s3(result[3]), .s26(result[26]), .s18(result[18]),
    .s10(result[10]), .s2(result[2]), .s25(result[25]), .s17(result[17]), .s9(result[9]), .s1(result[1]),
    .s24(result[24]), .s16(result[16]), .s8(result[8]), .s0(result[0]), .a31(A[31]), .a23(A[23]),
    .a15(A[15]), .a7(A[7]), .b31(B[31]), .b23(B[23]), .b15(B[15]), .b7(B[7]), .a30(A[30]), .a22(A[22]),
    .a14(A[14]), .a6(A[6]), .b30(B[30]), .b22(B[22]), .b14(B[14]), .b6(B[6]), .a29(A[29]), .a21(A[21]),
    .a13(A[13]), .a5(A[5]), .b29(B[29]), .b21(B[21]), .b13(B[13]), .b5(B[5]), .a28(A[28]), .a20(A[20]),
    .a12(A[12]), .a4(A[4]), .b28(B[28]), .b20(B[20]), .b12(B[12]), .b4(B[4]), .a27(A[27]), .a19(A[19]),
    .a11(A[11]), .a3(A[3]), .b27(B[27]), .b19(B[19]), .b11(B[11]), .b3(B[3]), .a26(A[26]), .a18(A[18]),
    .a10(A[10]), .a2(A[2]), .b26(B[26]), .b18(B[18]), .b10(B[10]), .b2(B[2]), .a25(A[25]), .a17(A[17]),
    .a9(A[9]), .a1(A[1]), .b25(B[25]), .b17(B[17]), .b9(B[9]), .b1(B[1]), .a24(A[24]), .a16(A[16]),
    .a8(A[8]), .a0(A[0]), .b24(B[24]), .b16(B[16]), .b8(B[8]), .b0(B[0]));  // open: cout
endmodule

module F_D (
  input  [31:0] PC,
  input  [31:0] Instruction,
  input  clk,
  input  reset,
  input  enable,
  output [31:0] Instruction_out,
  output [4:0] Rt,
  output [4:0] Rs,
  output [4:0] Rd,
  output [31:0] PC_out,
  output [4:0] Opcode_FD,
  output RdC,
  output BEXC,
  output RsC,
  output SwC,
  output SETXC,
  output [4:0] Rs2_FD,
  output [4:0] Rs1_FD
);

  wire ALUinB, ALUopAddC, BLTC, BNEC, DMld, DMwe, JalC, MEMwrite, or_1_out, PConeNC, PCRdC, PCTC, RstatusC,
       Rwe;
  wire [4:0] multiplexer_1_out, multiplexer_4_out, multiplexer_5_out;

  Multiplexer #(.width(5), .enable("false")) multiplexer_1 (
    .in0(Instruction_out[21:17]), .in1(Instruction_out[26:22]), .out(multiplexer_1_out), .sel(RdC));
  Multiplexer #(.width(5), .enable("false")) multiplexer_2 (
    .in0(multiplexer_1_out), .in1(5'b11110), .out(Rs1_FD), .sel(or_1_out));
  or or_1 (or_1_out, BEXC, SETXC);
  register_32 r_PC (.clk(clk), .\input (PC), .enable(enable), .\output (PC_out), .reset(reset));
  Multiplexer #(.width(5), .enable("false")) multiplexer_3 (
    .in0(multiplexer_4_out), .in1({5{1'b0}}), .out(Rs2_FD), .sel(BEXC));
  Multiplexer #(.width(5), .enable("false")) multiplexer_4 (
    .in0(multiplexer_5_out), .in1(Instruction_out[26:22]), .out(multiplexer_4_out), .sel(SwC));
  Multiplexer #(.width(5), .enable("false")) multiplexer_5 (
    .in0(Instruction_out[16:12]), .in1(Instruction_out[21:17]), .out(multiplexer_5_out), .sel(RsC));
  register_32 r_instruct (.clk(clk), .\input (Instruction), .enable(enable), .\output (Instruction_out), .reset(reset));
  control control_1 (
    .Opcode(Instruction_out[31:27]), .ALUop(Instruction_out[6:2]), .Rwe(Rwe), .ALUinB(ALUinB),
    .RstatusC(RstatusC), .JalC(JalC), .DMwe(DMwe), .DMld(DMld), .MEMwrite(MEMwrite), .Rdc(RdC),
    .PConeNC(PConeNC), .PCTC(PCTC), .PCRdC(PCRdC), .BNEC(BNEC), .BLTC(BLTC), .BEXC(BEXC), .RsC(RsC),
    .ALUopAddC(ALUopAddC), .SwC(SwC), .SETXC(SETXC));

  assign Opcode_FD = Instruction_out[31:27];
  assign Rd = Instruction_out[26:22];
  assign Rs = Instruction_out[21:17];
  assign Rt = Instruction_out[16:12];

  // Other names for the same wires on the sheet: instruct[31:0] = Instruction; Opcode[4:0] = Instruction_out[31:27];
  //   Immediate[16:0] = Instruction_out[16:0]; Target[26:0] = Instruction_out[26:0];
  //   Zeros[1:0] = Instruction_out[1:0]; ALUop[4:0] = Instruction_out[6:2]; Shamt[4:0] = Instruction_out[11:7]

  // Notes on the sheet:
  //   $rstatus
endmodule

module D_X (
  input  clk,
  input  reset,
  input  enable,
  input  [31:0] r1d,
  input  [31:0] r2d,
  input  [31:0] PC,
  input  [31:0] Instruction,
  output [31:0] r1d_out,
  output [31:0] r2d_out,
  output [16:0] Immediate,
  output [31:0] PC_out,
  output ALUinB,
  output PConeNC,
  output PCTC,
  output [26:0] Target,
  output PCRdC,
  output BNEC,
  output BLTC,
  output ALUopAddC,
  output SETXC,
  output [4:0] ALUop,
  output [31:0] Instruction_out,
  output BEXC_X,
  output [4:0] Shamt,
  output [4:0] Rs2_DX,
  output [4:0] Rs1_DX,
  output [4:0] Opcode_DX,
  output [4:0] Rd_DX_bypass
);

  wire DMld, DMwe, JalC, MEMwrite, or_1_out, RdC, RsC, RstatusC, Rwe, SwC, SwC_DX;
  wire [4:0] multiplexer_1_out, multiplexer_4_out, multiplexer_5_out, multiplexer_6_out;

  Multiplexer #(.width(5), .enable("false")) multiplexer_1 (
    .in0(Instruction_out[21:17]), .in1(Instruction_out[26:22]), .out(multiplexer_1_out), .sel(RdC));
  Multiplexer #(.width(5), .enable("false")) multiplexer_2 (
    .in0(multiplexer_1_out), .in1(5'b11110), .out(Rs1_DX), .sel(or_1_out));
  or or_1 (or_1_out, BEXC_X, SETXC);
  Multiplexer #(.width(5), .enable("false")) multiplexer_3 (
    .in0(multiplexer_4_out), .in1({5{1'b0}}), .out(Rs2_DX), .sel(BEXC_X));
  Multiplexer #(.width(5), .enable("false")) multiplexer_4 (
    .in0(multiplexer_5_out), .in1(Instruction_out[26:22]), .out(multiplexer_4_out), .sel(SwC));
  Multiplexer #(.width(5), .enable("false")) multiplexer_5 (
    .in0(Immediate[16:12]), .in1(Instruction_out[21:17]), .out(multiplexer_5_out), .sel(RsC));
  register_32 r_r1d (.clk(clk), .\input (r1d), .enable(enable), .\output (r1d_out), .reset(reset));
  register_32 r_r2d (.clk(clk), .\input (r2d), .enable(enable), .\output (r2d_out), .reset(reset));
  register_32 r_PC (.clk(clk), .\input (PC), .enable(enable), .\output (PC_out), .reset(reset));
  register_32 r_instruction (
    .clk(clk), .\input (Instruction), .enable(enable),
    .\output ({Instruction_out[31:17], Immediate[16:7], ALUop, Immediate[1:0]}), .reset(reset));
  Multiplexer #(.width(5), .enable("false")) multiplexer_6 (
    .in0(Instruction_out[26:22]), .in1(5'b11110), .out(multiplexer_6_out), .sel(RstatusC));
  Multiplexer #(.width(5), .enable("false")) multiplexer_7 (
    .in0(multiplexer_6_out), .in1({5{1'b1}}), .out(Rd_DX_bypass), .sel(JalC));
  control control_1 (
    .Opcode(Instruction_out[31:27]), .ALUop(ALUop), .Rwe(Rwe), .ALUinB(ALUinB), .RstatusC(RstatusC),
    .JalC(JalC), .DMwe(DMwe), .DMld(DMld), .MEMwrite(MEMwrite), .Rdc(RdC), .PConeNC(PConeNC), .PCTC(PCTC),
    .PCRdC(PCRdC), .BNEC(BNEC), .BLTC(BLTC), .BEXC(BEXC_X), .RsC(RsC), .ALUopAddC(ALUopAddC), .SwC(SwC),
    .SETXC(SETXC));
  or or_2 (SwC_DX, SwC, BNEC, BLTC);

  assign Immediate[6:2] = ALUop;
  assign Instruction_out[16:0] = {Immediate[16:7], ALUop, Immediate[1:0]};
  assign Opcode_DX = Instruction_out[31:27];
  assign Shamt = Immediate[11:7];
  assign Target = {Instruction_out[26:17], Immediate[16:7], ALUop, Immediate[1:0]};

  // Other names for the same wires on the sheet: BEXC = BEXC_X; Opcode[4:0] = Instruction_out[31:27];
  //   Immediate_t[16:0] = {Immediate[16:7], ALUop, Immediate[1:0]}; Zeros[1:0] = Immediate[1:0];
  //   Rt[4:0] = Immediate[16:12]; Rs[4:0] = Instruction_out[21:17]; Rd[4:0] = Instruction_out[26:22]

  // Notes on the sheet:
  //   $rstatus
  //   $rstatus
  //   $r31
endmodule

module X_M (
  input  clk,
  input  reset,
  input  enable,
  input  [31:0] PC,
  input  [31:0] Instruction,
  input  [31:0] r2d,
  input  [31:0] alu_out,
  input  ovf,
  output [31:0] PC_out,
  output DMwe,
  output DMld,
  output MEMwrite,
  output [31:0] Instruction_out,
  output SwC_XM,
  output [31:0] r2d_out,
  output [31:0] alu_out_out,
  output [4:0] Rd_XM_bypass
);

  wire ALUinB, ALUopAddC, BEXC, BLTC, BNEC, comparator_1_eq, comparator_2_eq, comparator_3_eq,
       comparator_5_eq, comparator_6_eq, comparator_7_eq, JalC, PConeNC, PCRdC, PCTC, r_ovf, RdC, RsC,
       RstatusC, Rwe, SwC;
  wire [4:0] and_1_out, multiplexer_1_out, multiplexer_2_out;
  wire [26:22] r_instruction_output;
  wire [31:0] r_alu_out_output, rstatus_ovf;

  register_32 r_PC (.clk(clk), .\input (PC), .enable(enable), .\output (PC_out), .reset(reset));
  register_32 r_instruction (
    .clk(clk), .\input (Instruction), .enable(enable),
    .\output ({Instruction_out[31:27], r_instruction_output, Instruction_out[21:0]}), .reset(reset));
  register_32 r_r2d (.clk(clk), .\input (r2d), .enable(enable), .\output (r2d_out), .reset(reset));
  register_32 r_alu_out (.clk(clk), .\input (alu_out), .enable(enable), .\output (r_alu_out_output), .reset(reset));
  D_Flip_Flop u_r_ovf (.clk(clk), .D(ovf), .Q(r_ovf), .en(enable), .reset(reset));  // open: Qn, preset
  Multiplexer #(.width(5), .enable("false")) multiplexer_1 (
    .in0(Instruction_out[26:22]), .in1(5'b11110), .out(multiplexer_1_out), .sel(RstatusC));
  Multiplexer #(.width(5), .enable("false")) multiplexer_2 (
    .in0(multiplexer_1_out), .in1({5{1'b1}}), .out(multiplexer_2_out), .sel(JalC));
  Multiplexer #(.width(32), .enable("false")) multiplexer_3 (
    .in0(r_alu_out_output), .in1(rstatus_ovf), .out(alu_out_out), .sel(r_ovf));
  Multiplexer #(.width(5), .enable("false")) multiplexer_4 (
    .in0(multiplexer_2_out), .in1(5'b11110), .out(Rd_XM_bypass), .sel(r_ovf));
  Comparator #(.width(5)) comparator_1 (.a(Rd_XM_bypass), .b({5{1'b0}}), .eq(comparator_1_eq));  // open: gt, lt
  control control_1 (
    .Opcode(Instruction_out[31:27]), .ALUop(Instruction_out[6:2]), .Rwe(Rwe), .ALUinB(ALUinB),
    .RstatusC(RstatusC), .JalC(JalC), .DMwe(DMwe), .DMld(DMld), .MEMwrite(MEMwrite), .Rdc(RdC),
    .PConeNC(PConeNC), .PCTC(PCTC), .PCRdC(PCRdC), .BNEC(BNEC), .BLTC(BLTC), .BEXC(BEXC), .RsC(RsC),
    .ALUopAddC(ALUopAddC), .SwC(SwC));  // open: SETXC
  or or_1 (SwC_XM, SwC, comparator_1_eq, BNEC, BEXC, BLTC);
  Multiplexer #(.width(5), .enable("false")) multiplexer_5 (
    .in0(r_instruction_output), .in1(5'b11110), .out(Instruction_out[26:22]), .sel(r_ovf));
  Comparator #(.width(5)) comparator_2 (
    .a(Instruction_out[31:27]), .b({5{1'b0}}), .eq(comparator_2_eq));  // open: gt, lt
  Comparator #(.width(5)) comparator_3 (.a(Instruction_out[6:2]), .b({5{1'b0}}), .eq(comparator_3_eq));  // open: gt, lt
  Comparator #(.width(5)) comparator_4 (.a(Instruction_out[31:27]), .b(5'b00101), .eq(and_1_out[1]));  // open: gt, lt
  Comparator #(.width(5)) comparator_5 (.a(Instruction_out[6:2]), .b(5'b00001), .eq(comparator_5_eq));  // open: gt, lt
  Comparator #(.width(5)) comparator_6 (.a(Instruction_out[6:2]), .b(5'b00110), .eq(comparator_6_eq));  // open: gt, lt
  Comparator #(.width(5)) comparator_7 (.a(Instruction_out[6:2]), .b(5'b00111), .eq(comparator_7_eq));  // open: gt, lt
  and and_1 (and_1_out[0], comparator_2_eq, comparator_3_eq);
  and and_2 (and_1_out[2], comparator_2_eq, comparator_5_eq);
  and and_3 (and_1_out[3], comparator_2_eq, comparator_6_eq);
  and and_4 (and_1_out[4], comparator_2_eq, comparator_7_eq);
  Multiplexer #(.select(5), .width(32), .enable("false")) multiplexer_6 (
    .in1(32'h1), .in2(32'h2), .in4(32'h3), .in8(32'h4), .in16(32'h5), .out(rstatus_ovf), .sel(and_1_out));  // open: in0, in3, in5, in6, in7, in9, in10, in11, in12, in13, in14, in15, in17, in18, in19, in20, in21, in22, in23, in24, in25, in26, in27, in28, in29, in30, in31

  // Other names for the same wires on the sheet: Opcode[4:0] = Instruction_out[31:27];
  //   Immediate[16:0] = Instruction_out[16:0]; Target[26:0] = Instruction_out[26:0];
  //   Zeros[1:0] = Instruction_out[1:0]; ALUop[4:0] = Instruction_out[6:2]; Shamt[4:0] = Instruction_out[11:7];
  //   Rt[4:0] = Instruction_out[16:12]; Rs[4:0] = Instruction_out[21:17]; Rd[4:0] = Instruction_out[26:22]

  // Notes on the sheet:
  //   $rstatus
  //   $r31
endmodule

module M_W (
  input  clk,
  input  reset,
  input  enable,
  input  [31:0] PC,
  input  [31:0] Instruction,
  input  [31:0] wdata,
  output Rwe,
  output JalC,
  output [31:0] PC_out,
  output RstatusC,
  output [4:0] Rd_MW,
  output [31:0] Instruction_out,
  output [31:0] wdata_out,
  output [4:0] Rd_MW_bypass,
  output SwC_MW
);

  wire ALUinB, ALUopAddC, BEXC, BLTC, BNEC, comparator_1_eq, DMld, DMwe, MEMwrite, PConeNC, PCRdC, PCTC, RdC,
       RsC, SwC;
  wire [4:0] multiplexer_1_out;

  register_32 r_PC (.clk(clk), .\input (PC), .enable(enable), .\output (PC_out), .reset(reset));
  register_32 r_instruction (
    .clk(clk), .\input (Instruction), .enable(enable), .\output (Instruction_out), .reset(reset));
  register_32 r_instruction_2 (.clk(clk), .\input (wdata), .enable(enable), .\output (wdata_out), .reset(reset));
  Multiplexer #(.width(5), .enable("false")) multiplexer_1 (
    .in0(Instruction_out[26:22]), .in1(5'b10111), .out(multiplexer_1_out), .sel(RstatusC));
  Multiplexer #(.width(5), .enable("false")) multiplexer_2 (
    .in0(multiplexer_1_out), .in1({5{1'b1}}), .out(Rd_MW_bypass), .sel(JalC));
  Comparator #(.width(5)) comparator_1 (.a(Rd_MW_bypass), .b({5{1'b0}}), .eq(comparator_1_eq));  // open: gt, lt
  control control_1 (
    .Opcode(Instruction_out[31:27]), .ALUop(Instruction_out[6:2]), .Rwe(Rwe), .ALUinB(ALUinB),
    .RstatusC(RstatusC), .JalC(JalC), .DMwe(DMwe), .DMld(DMld), .MEMwrite(MEMwrite), .Rdc(RdC),
    .PConeNC(PConeNC), .PCTC(PCTC), .PCRdC(PCRdC), .BNEC(BNEC), .BLTC(BLTC), .BEXC(BEXC), .RsC(RsC),
    .ALUopAddC(ALUopAddC), .SwC(SwC));  // open: SETXC
  or or_1 (SwC_MW, SwC, BEXC, BLTC, comparator_1_eq, BNEC);

  assign Rd_MW = Instruction_out[26:22];

  // Other names for the same wires on the sheet: Opcode[4:0] = Instruction_out[31:27];
  //   Immediate[16:0] = Instruction_out[16:0]; Target[26:0] = Instruction_out[26:0];
  //   Zeros[1:0] = Instruction_out[1:0]; ALUop[4:0] = Instruction_out[6:2]; Shamt[4:0] = Instruction_out[11:7];
  //   Rt[4:0] = Instruction_out[16:12]; Rs[4:0] = Instruction_out[21:17]; Rd[4:0] = Instruction_out[26:22]

  // Notes on the sheet:
  //   $rstatus
  //   $r31
endmodule

module four_count (
  input  clk,
  input  start_signal,
  input  enable,
  input  reset,
  output out
);

  wire d_ff_1_q, d_ff_2_q, d_ff_3_q;

  D_Flip_Flop d_ff_1 (.clk(clk), .D(start_signal), .Q(d_ff_1_q), .en(enable), .reset(reset));  // open: Qn, preset
  D_Flip_Flop d_ff_2 (.clk(clk), .D(d_ff_1_q), .Q(d_ff_2_q), .en(enable), .reset(reset));  // open: Qn, preset
  D_Flip_Flop d_ff_3 (.clk(clk), .D(d_ff_2_q), .Q(d_ff_3_q), .en(enable), .reset(reset));  // open: Qn, preset
  D_Flip_Flop d_ff_4 (.clk(clk), .D(d_ff_3_q), .Q(out), .en(enable), .reset(reset));  // open: Qn, preset
endmodule

module multdiv_behavioral (
  input  clk,
  input  mult_start,
  input  div_start,
  input  [31:0] A,
  input  [31:0] B,
  output [31:0] out,
  output mult_rdy,
  output div_rdy
);

  wire or_2_out, res;
  wire [31:0] divider_1_out, multiplier_1_out;

  Multiplier #(.width(32)) multiplier_1 (.a(A), .b(B), .out(multiplier_1_out));  // open: cin, cout
  Divider #(.width(32)) divider_1 (.a(A), .b(B), .out(divider_1_out));  // open: upper, rem
  Multiplexer #(.width(32), .enable("false")) multiplexer_1 (
    .in0(multiplier_1_out), .in1(divider_1_out), .out(out), .sel(div_rdy));
  or or_1 (res, mult_start, div_start);
  four_count four_count_1 (.clk(clk), .start_signal(mult_start), .enable(1'b1), .out(mult_rdy));  // open: reset
  four_count four_count_2 (.clk(clk), .start_signal(div_start), .enable(1'b1), .out(div_rdy));  // open: reset
  or or_2 (or_2_out, mult_rdy, div_rdy);
endmodule
